// Logisim project cpu_benchmark.circ as structural Verilog: 7 circuits, main circuit cpu
module cpu (
);

  wire _5ExtImm, and_1_out, clock_1_out, comparator_1_eq, controler_1__16extimm, controler_1_jal,
       controler_1_lw, controler_1_regwrite, controler_1_sextimm, controler_1_sw, controler_1_syscall,
       enchange, ex_mem_1__16extimmout, ex_mem_1_jalout, ex_mem_1_lwout, ex_mem_1_sextimmout, ex_mem_1_swout,
       ex_mem_1_sysout, ex_mem_1_weout, Go, halt, id_ex_1__5extimmout, id_ex_1__16extimmout, id_ex_1_jalout,
       id_ex_1_lwout, id_ex_1_sextimmout, id_ex_1_swout, id_ex_1_sysout, id_ex_1_weout, IR1, IR2, IR3,
       not_1_out, not_2_out, or_1_out, registerfile_1_p3, RST, SH, syscall, W1, W2, W3;
  wire [3:0] controler_1_aluop, id_ex_1_aluopout;
  wire [4:0] ex_mem_1_rdout, ex_mem_1_rtout, id_ex_1_rdout, id_ex_1_rtout, rA_t, rB_t, registerfile_1_p4, Rs,
       Rt;
  wire [11:0] EX_PC, ID_PC, IF_PC, WB_PC;
  wire [15:0] counter_1_q, \load_use次数 , \总周期数 , \插入气泡数 , \无条件分支指令数 , \有条件分支成功跳转 , \有条件分支指令数 ;
  wire [31:0] alu_1_result, bit_extender_1_out, bit_extender_2_out, ex_mem_1_pcout, ex_mem_1_rbout,
       ex_mem_1_rout, id_ex_1_offsetout, id_ex_1_pcout, id_ex_1_raout, id_ex_1_rbout, if_id_1_insout,
       if_id_1_pcout, multiplexer_3_out, multiplexer_4_out, multiplexer_5_out, npc_1_nextpc, PC_q, RA,
       ram_1_data, RB, registerfile_1_p1, rom_1_data, SyscallOut;

  Button \u_总复位  (.out(RST));
  Button _1 (.out(IR1));
  Button _2 (.out(IR2));
  Button _3 (.out(IR3));
  Button \u_继续运行  (.out(Go));
  LED led_1 (.in(W1));
  LED led_2 (.in(W2));
  LED led_3 (.in(W3));
  // Probe on IF_PC
  Clock clock_1 (.out(clock_1_out));
  not not_1 (not_1_out, halt);
  Hex_Digit_Display hex_digit_display_1 (.value(SyscallOut[31:28]));  // open: dp
  Register #(.width(32)) a0 (.D(RB), .en(and_1_out), .Q(SyscallOut), .clk(clock_1_out), .clr(RST));
  and and_1 (and_1_out, syscall, not_2_out);
  Hex_Digit_Display hex_digit_display_2 (.value(SyscallOut[23:20]));  // open: dp
  Hex_Digit_Display hex_digit_display_3 (.value(SyscallOut[27:24]));  // open: dp
  // Probe on ID_PC
  not not_2 (not_2_out, halt);
  Hex_Digit_Display hex_digit_display_4 (.value(SyscallOut[15:12]));  // open: dp
  Hex_Digit_Display hex_digit_display_5 (.value(SyscallOut[19:16]));  // open: dp
  NPC npc_1 (
    .Reset(RST), .CLK(clock_1_out), .IM(rom_1_data), .PC(PC_q), .RegRS(RA), .RegRT(RB),
    .OFFSET(multiplexer_3_out), .NextPC(npc_1_nextpc), .unconditional(\无条件分支指令数 ), .conditional(\有条件分支指令数 ),
    .conditionalsucces(\有条件分支成功跳转 ));
  Counter #(.width(16), .max('hffff)) counter_1 (
    .count(not_1_out), .Q(counter_1_q), .clk(clock_1_out), .clr(RST));  // open: load, D, carry
  Hex_Digit_Display hex_digit_display_6 (.value(SyscallOut[7:4]));  // open: dp
  Hex_Digit_Display hex_digit_display_7 (.value(SyscallOut[11:8]));  // open: dp
  // Probe on EX_PC
  Adder #(.width(16)) adder_1 (.a(counter_1_q), .b({{15{1'b0}}, halt}), .out(\总周期数 ));  // open: cin, cout
  Comparator #(.width(32)) comparator_1 (.a(32'ha), .b(RA), .eq(comparator_1_eq));  // open: gt, lt
  Hex_Digit_Display hex_digit_display_8 (.value(SyscallOut[3:0]));  // open: dp
  // Probe on EX_PC
  Register #(.width(32)) PC (.D(npc_1_nextpc), .en(not_1_out), .Q(PC_q), .clk(clock_1_out), .clr(RST));
  and and_2 (halt, comparator_1_eq, syscall);
  Multiplexer #(.width(5), .enable("false")) multiplexer_1 (.in0(Rs), .in1(5'b00010), .out(rA_t), .sel(syscall));
  // Probe on \总周期数 
  // Probe on \无条件分支指令数 
  // Probe on \有条件分支成功跳转 
  // Probe on \load_use次数 
  // Probe on \插入气泡数 
  // Probe on WB_PC
  ROM #(.addrWidth(10), .dataWidth(32)) rom_1 (.addr(PC_q[11:2]), .data(rom_1_data));  // open: sel
  Multiplexer #(.width(5), .enable("false")) multiplexer_2 (.in0(Rt), .in1(5'b00100), .out(rB_t), .sel(syscall));
  IF_ID if_id_1 (
    .Insin(rom_1_data), .PCin(PC_q), .clk(clock_1_out),
    .Insout({if_id_1_insout[31:26], Rs, Rt, if_id_1_insout[15:0]}), .PCout(if_id_1_pcout), .rst(RST),
    .in_5(halt));
  assign bit_extender_1_out = {{16{if_id_1_insout[15]}}, if_id_1_insout[15:0]};  // Bit_Extender bit_extender_1
  assign bit_extender_2_out = {{27{1'b0}}, if_id_1_insout[10:6]};  // Bit_Extender bit_extender_2
  controler controler_1 (
    .operator(if_id_1_insout[31:26]), .func(if_id_1_insout[5:0]), .AluOp(controler_1_aluop),
    .LW(controler_1_lw), ._16ExtImm(controler_1__16extimm), .JAL(controler_1_jal),
    .syscall(controler_1_syscall), .SW(controler_1_sw), .SExtImm(controler_1_sextimm), ._5ExtImm(_5ExtImm),
    .SH(SH), .RegWrite(controler_1_regwrite), .enchange(enchange));
  Multiplexer #(.width(32), .enable("false")) multiplexer_3 (
    .in0(bit_extender_1_out), .in1(bit_extender_2_out), .out(multiplexer_3_out), .sel(_5ExtImm));
  // Probe on RA
  // RegisterFile registerfile_1: pin names not known; wires that end beside it: registerfile_1_p1, clock_1_out, registerfile_1_p3, registerfile_1_p4, rA_t, rB_t, RA, RB
  ID_EX id_ex_1 (
    .RAin(RA), .RBin(RB), ._16ExtImmin(controler_1__16extimm), .SextImmin(controler_1_sextimm),
    ._5extImmin(_5ExtImm), .SWin(controler_1_sw), .ALUOPin(controler_1_aluop), .clk(clock_1_out),
    .RAout(id_ex_1_raout), .RBout(id_ex_1_rbout), ._16ExtImmout(id_ex_1__16extimmout),
    .SextImmout(id_ex_1_sextimmout), ._5extImmout(id_ex_1__5extimmout), .SWout(id_ex_1_swout),
    .ALUOPout(id_ex_1_aluopout), .PCin(if_id_1_pcout), .PCout(id_ex_1_pcout), .LWin(controler_1_lw),
    .LWout(id_ex_1_lwout), .JALin(controler_1_jal), .JALout(id_ex_1_jalout), .RDin(if_id_1_insout[15:11]),
    .RDout(id_ex_1_rdout), .RTin(Rt), .RTout(id_ex_1_rtout), .WEin(controler_1_regwrite),
    .WEout(id_ex_1_weout), .OFFSETin(multiplexer_3_out), .OFFsetout(id_ex_1_offsetout), .rst(RST),
    .halt(halt), .SYSin(controler_1_syscall), .SYSout(id_ex_1_sysout));  // open: RAin_2, RAout_2, RBin_2, RBout_2
  Multiplexer #(.width(32), .enable("false")) multiplexer_4 (
    .in0(id_ex_1_raout), .in1(id_ex_1_rbout), .out(multiplexer_4_out), .sel(id_ex_1__5extimmout));
  ALU alu_1 (
    .AluOP(id_ex_1_aluopout), .X(multiplexer_4_out), .Result(alu_1_result), .Y(multiplexer_5_out));  // open: Equal, Signed_Overflow, Result_2, UnSigned_Overflow
  Multiplexer #(.width(32), .enable("false")) multiplexer_5 (
    .in0(id_ex_1_rbout), .in1(id_ex_1_offsetout), .out(multiplexer_5_out), .sel(or_1_out));
  or or_1 (or_1_out, id_ex_1__16extimmout, id_ex_1_sextimmout, id_ex_1__5extimmout);
  EX_MEM ex_mem_1 (
    .LWin(id_ex_1_lwout), .LWout(ex_mem_1_lwout), .Rin(alu_1_result), .Rout(ex_mem_1_rout),
    .JALin(id_ex_1_jalout), .JALout(ex_mem_1_jalout), .RBin(id_ex_1_rbout), .RBout(ex_mem_1_rbout),
    ._16ExtImmin(id_ex_1__16extimmout), ._16ExtImmout(ex_mem_1__16extimmout), .SextImmin(id_ex_1_sextimmout),
    .SextImmout(ex_mem_1_sextimmout), ._5extImmin(id_ex_1__5extimmout), .SWin(id_ex_1_swout),
    .SWout(ex_mem_1_swout), .PCin(id_ex_1_pcout), .PCout(ex_mem_1_pcout), .clk(clock_1_out),
    .RDin(id_ex_1_rdout), .RDout(ex_mem_1_rdout), .RTin(id_ex_1_rtout), .RTout(ex_mem_1_rtout),
    .WEin(id_ex_1_weout), .WEout(ex_mem_1_weout), .rst(RST), .halt(halt), .SYSin(id_ex_1_sysout),
    .SYSout(ex_mem_1_sysout));  // open: _5extImmout, ALUOPin, ALUOPout, RAin, RAout, RBin_2, RBout_2
  RAM #(.addrWidth(12), .dataWidth(32), .bus("separate")) ram_1 (
    .addr(ex_mem_1_rout[13:2]), .din(ex_mem_1_rbout), .data(ram_1_data), .str(ex_mem_1_swout), .sel(1'b1),
    .clk(clock_1_out), .ld(1'b1), .clr(RST));
  MEM_WB mem_wb_1 (
    .Rin(ex_mem_1_rout), .DATAin(ram_1_data), .clk(clock_1_out), .PCin(ex_mem_1_pcout),
    .Wout(registerfile_1_p1), .LWin(ex_mem_1_lwout), .JALin(ex_mem_1_jalout),
    ._16ExtImmin(ex_mem_1__16extimmout), .SextImmin(ex_mem_1_sextimmout), .RDin(ex_mem_1_rdout),
    .RTin(ex_mem_1_rtout), .rWin(registerfile_1_p4), .WEin(ex_mem_1_weout), .WEout(registerfile_1_p3),
    .rst(RST), .halt(halt), .SYSin(ex_mem_1_sysout), .SYSout(syscall));  // open: RAin, RBin, RBout, RAout

  // Notes on the sheet:
  //   中断源
  //   中断请求指示
  //   数码管输出应该用寄存器锁存，否则显示数据只能一闪而过
  //   可以通过项目增加Logisim库的方式将前几次实验完成的电路作为子电路引入到本电路中使用
  //   数码管输出
  //   总复位信号应将除ROM以外所有存储组件全部清零
  //   指令存储器
  //   contents of rom_1 (hex, n*v repeats v):
  //   20100000 20110000 20120000 20130000 36100000 36310001 36520002 36730003 ae100000 ae110004 ae120008
  //   ae13000c 2002000a 20110000 20120000 20130000 c
  //   寄存器文件
endmodule

module controler (
  input  [5:0] operator,
  input  [5:0] func,
  output syscall,
  output _16ExtImm,
  output SExtImm,
  output _5ExtImm,
  output [3:0] AluOp,
  output LW,
  output SW,
  output SH,
  output RegWrite,
  output enchange,
  output JAL
);

  wire ADD, ADDI, ADDIU, ADDU, AND, ANDI, BEQ, BGTZ, BNE, comparator_2_eq, comparator_3_eq, comparator_6_eq,
       comparator_8_eq, comparator_9_eq, comparator_10_eq, comparator_11_eq, comparator_12_eq,
       comparator_13_eq, comparator_15_eq, comparator_16_eq, comparator_17_eq, comparator_19_eq,
       comparator_27_eq, comparator_28_eq, JR, NOR, OR, ORI, R1, SLL, SLLV, SLT, SLTI, SLTU, SRA, SRL, SRLV,
       SUB;
  wire [3:0] and_16_out, and_17_out, and_18_out, and_19_out, and_20_out, and_21_out, and_22_out, and_23_out,
       and_24_out, and_25_out;
  wire [3:3] or_1_out, or_2_out, or_3_out, or_4_out, or_5_out, or_6_out;

  Comparator #(.width(6)) comparator_1 (.a(operator), .b({6{1'b0}}), .eq(R1));  // open: gt, lt
  Comparator #(.width(6)) comparator_2 (.a(func), .b(6'b100000), .eq(comparator_2_eq));  // open: gt, lt
  Comparator #(.width(6)) comparator_3 (.a(func), .b(6'b100001), .eq(comparator_3_eq));  // open: gt, lt
  Comparator #(.width(6)) comparator_4 (.a(operator), .b(6'b001000), .eq(ADDI));  // open: gt, lt
  Comparator #(.width(6)) comparator_5 (.a(operator), .b(6'b001001), .eq(ADDIU));  // open: gt, lt
  Comparator #(.width(6)) comparator_6 (.a(func), .b(6'b100100), .eq(comparator_6_eq));  // open: gt, lt
  Comparator #(.width(6)) comparator_7 (.a(operator), .b(6'b001100), .eq(ANDI));  // open: gt, lt
  Comparator #(.width(6)) comparator_8 (.a(func), .b({6{1'b0}}), .eq(comparator_8_eq));  // open: gt, lt
  Comparator #(.width(6)) comparator_9 (.a(func), .b(6'b000100), .eq(comparator_9_eq));  // open: gt, lt
  Comparator #(.width(6)) comparator_10 (.a(func), .b(6'b000010), .eq(comparator_10_eq));  // open: gt, lt
  Comparator #(.width(6)) comparator_11 (.a(func), .b(6'b000110), .eq(comparator_11_eq));  // open: gt, lt
  Comparator #(.width(6)) comparator_12 (.a(func), .b(6'b000011), .eq(comparator_12_eq));  // open: gt, lt
  Comparator #(.width(6)) comparator_13 (.a(func), .b(6'b100101), .eq(comparator_13_eq));  // open: gt, lt
  Comparator #(.width(6)) comparator_14 (.a(operator), .b(6'b001101), .eq(ORI));  // open: gt, lt
  Comparator #(.width(6)) comparator_15 (.a(func), .b(6'b100111), .eq(comparator_15_eq));  // open: gt, lt
  Comparator #(.width(6)) comparator_16 (.a(func), .b(6'b101010), .eq(comparator_16_eq));  // open: gt, lt
  Comparator #(.width(6)) comparator_17 (.a(func), .b(6'b101011), .eq(comparator_17_eq));  // open: gt, lt
  Comparator #(.width(6)) comparator_18 (.a(operator), .b(6'b001010), .eq(SLTI));  // open: gt, lt
  Comparator #(.width(6)) comparator_19 (.a(func), .b(6'b100010), .eq(comparator_19_eq));  // open: gt, lt
  Comparator #(.width(6)) comparator_20 (.a(operator), .b(6'b000101), .eq(BNE));  // open: gt, lt
  Comparator #(.width(6)) comparator_21 (.a(operator), .b(6'b000111), .eq(BGTZ));  // open: gt, lt
  Comparator #(.width(6)) comparator_22 (.a(operator), .b(6'b000100), .eq(BEQ));  // open: gt, lt
  Comparator #(.width(6)) comparator_23 (.a(operator), .b(6'b100011), .eq(LW));  // open: gt, lt
  Comparator #(.width(6)) comparator_24 (.a(operator), .b(6'b101011), .eq(SW));  // open: gt, lt
  Comparator #(.width(6)) comparator_25 (.a(operator), .b(6'b101001), .eq(SH));  // open: gt, lt
  and and_1 (ADD, R1, comparator_2_eq);
  and and_2 (ADDU, R1, comparator_3_eq);
  and and_3 (AND, R1, comparator_6_eq);
  and and_4 (SLL, R1, comparator_8_eq);
  and and_5 (SLLV, R1, comparator_9_eq);
  and and_6 (SRL, R1, comparator_10_eq);
  and and_7 (SRLV, R1, comparator_11_eq);
  and and_8 (SRA, R1, comparator_12_eq);
  and and_9 (OR, R1, comparator_13_eq);
  and and_10 (NOR, R1, comparator_15_eq);
  and and_11 (SLT, R1, comparator_16_eq);
  and and_12 (SLTU, R1, comparator_17_eq);
  and and_13 (SUB, R1, comparator_19_eq);
  Comparator #(.width(6)) comparator_26 (.a(operator), .b(6'b000011), .eq(JAL));  // open: gt, lt
  Comparator #(.width(6)) comparator_27 (.a(func), .b(6'b001000), .eq(comparator_27_eq));  // open: gt, lt
  Comparator #(.width(6)) comparator_28 (.a(func), .b(6'b001100), .eq(comparator_28_eq));  // open: gt, lt
  and and_14 (JR, R1, comparator_27_eq);
  and and_15 (syscall, R1, comparator_28_eq);
  or or_1 (or_1_out[3], ADD, ADDI, ADDU, ADDIU, SW, LW, SH);
  or or_2 (or_2_out[3], AND, ANDI);
  or or_3 (or_3_out[3], OR, ORI);
  or or_4 (or_4_out[3], SLL, SLLV);
  or or_5 (or_5_out[3], SLT, SLTI);
  or or_6 (or_6_out[3], SRL, SRLV);
  assign and_16_out = 4'b0101 & {4{or_1_out[3]}};  // AND_Gate and_16, 4 bits wide
  assign and_17_out = 4'b0111 & {4{or_2_out[3]}};  // AND_Gate and_17, 4 bits wide
  assign and_18_out = 4'b1000 & {4{or_3_out[3]}};  // AND_Gate and_18, 4 bits wide
  assign and_19_out = 4'b0000 & {4{or_4_out[3]}};  // AND_Gate and_19, 4 bits wide
  assign and_20_out = 4'b1010 & {4{NOR}};  // AND_Gate and_20, 4 bits wide
  assign and_21_out = 4'b0001 & {4{SRA}};  // AND_Gate and_21, 4 bits wide
  assign and_22_out = 4'b1011 & {4{or_5_out[3]}};  // AND_Gate and_22, 4 bits wide
  assign and_23_out = 4'b1100 & {4{SLTU}};  // AND_Gate and_23, 4 bits wide
  assign and_24_out = 4'b0110 & {4{SUB}};  // AND_Gate and_24, 4 bits wide
  assign and_25_out = 4'b0010 & {4{or_6_out[3]}};  // AND_Gate and_25, 4 bits wide
  assign AluOp = and_16_out | and_17_out | and_18_out | and_19_out | and_20_out | and_21_out | and_22_out | and_23_out | and_24_out | and_25_out;  // OR_Gate or_7, 4 bits wide
  or or_8 (_16ExtImm, ANDI, ORI);
  or or_9 (SExtImm, ADDI, ADDIU, LW, SW, SH, BNE, BGTZ, BEQ, SLTI);
  or or_10 (_5ExtImm, SLL, SRA, SRL);
  or or_11 (enchange, SRLV, SLLV);
  or or_12 (RegWrite, SRLV, ADD, ADDU, ADDI, ADDIU, AND, ANDI, SLL, SLLV, SRL, SRA, OR, ORI, NOR, SLT, SLTU, SLTI, SUB, JAL, LW);

  // Other names for the same wires on the sheet: operate[5:0] = operator; sllv_srlv = enchange
endmodule

module NPC (
  input  Reset,
  input  CLK,
  input  [31:0] IM,
  input  [31:0] PC,
  input  [31:0] RegRS,
  input  [31:0] RegRT,
  input  [31:0] OFFSET,
  output [31:0] NextPC,
  output [15:0] unconditional,
  output [15:0] conditional,
  output [15:0] conditionalsucces
);

  wire and_3_out, and_4_out, and_5_out, BEQ, BGTZ, BNE, comparator_1_eq, comparator_2_eq, comparator_3_eq,
       comparator_4_eq, comparator_4_gt, comparator_10_eq, halt, J, JAL, JR, not_1_out, not_2_out, or_3_out,
       or_4_out, syscall;
  wire [1:0] or_2_out;
  wire [31:0] adder_1_out, adder_2_out, multiplexer_1_out, multiplexer_2_out;

  Multiplexer #(.width(32), .enable("false")) multiplexer_1 (
    .in0(RegRT), .in1({32{1'b0}}), .out(multiplexer_1_out), .sel(BGTZ));
  // Probe on PC
  Comparator #(.width(6)) comparator_1 (.a(IM[5:0]), .b(6'b001000), .eq(comparator_1_eq));  // open: gt, lt
  Comparator #(.width(6)) comparator_2 (.a(IM[31:26]), .b({6{1'b0}}), .eq(comparator_2_eq));  // open: gt, lt
  Comparator #(.width(6)) comparator_3 (.a(IM[5:0]), .b(6'b001100), .eq(comparator_3_eq));  // open: gt, lt
  Adder #(.width(32)) adder_1 (.a(PC), .b(32'h4), .out(adder_1_out));  // open: cin, cout
  Multiplexer #(.width(32), .enable("false")) multiplexer_2 (
    .in0({PC[31:28], IM[25:0], 2'b00}), .in1(RegRS), .out(multiplexer_2_out), .sel(JR));
  Adder #(.width(32)) adder_2 (.a({OFFSET[29:0], 2'b00}), .b(adder_1_out), .out(adder_2_out));  // open: cin, cout
  Comparator #(.width(32)) comparator_4 (
    .a(RegRS), .b(multiplexer_1_out), .gt(comparator_4_gt), .eq(comparator_4_eq));  // open: lt
  Comparator #(.width(6)) comparator_5 (.a(IM[31:26]), .b(6'b000010), .eq(J));  // open: gt, lt
  Comparator #(.width(6)) comparator_6 (.a(IM[31:26]), .b(6'b000011), .eq(JAL));  // open: gt, lt
  and and_1 (JR, comparator_1_eq, comparator_2_eq);
  and and_2 (syscall, comparator_2_eq, comparator_3_eq);
  not not_1 (not_1_out, comparator_4_eq);
  and and_3 (and_3_out, BGTZ, comparator_4_gt);
  and and_4 (and_4_out, not_1_out, BNE);
  and and_5 (and_5_out, comparator_4_eq, BEQ);
  Multiplexer #(.select(2), .width(32)) multiplexer_3 (
    .in0(adder_1_out), .in1(adder_2_out), .in2(multiplexer_2_out), .out(NextPC), .sel(or_2_out),
    .en(not_2_out));  // open: in3
  or or_1 (or_2_out[1], J, JAL, JR);
  or or_2 (or_2_out[0], and_3_out, and_4_out, and_5_out);
  Comparator #(.width(6)) comparator_7 (.a(IM[31:26]), .b(6'b000101), .eq(BNE));  // open: gt, lt
  Comparator #(.width(6)) comparator_8 (.a(IM[31:26]), .b(6'b000111), .eq(BGTZ));  // open: gt, lt
  Comparator #(.width(6)) comparator_9 (.a(IM[31:26]), .b(6'b000100), .eq(BEQ));  // open: gt, lt
  Comparator #(.width(32)) comparator_10 (.a(RegRS), .b(32'ha), .eq(comparator_10_eq));  // open: gt, lt
  not not_2 (not_2_out, Reset);
  and and_6 (halt, comparator_10_eq, syscall);
  or or_3 (or_3_out, J, JAL, JR);
  or or_4 (or_4_out, BNE, BGTZ, BEQ);
  Counter #(.width(16), .max('hffff)) counter_1 (
    .count(or_3_out), .Q(unconditional), .clk(CLK), .clr(Reset));  // open: load, D, carry
  Counter #(.width(16), .max('hffff)) counter_2 (
    .count(or_4_out), .Q(conditional), .clk(CLK), .clr(Reset));  // open: load, D, carry
  Counter #(.width(16), .max('hffff)) counter_3 (
    .count(or_2_out[0]), .Q(conditionalsucces), .clk(CLK), .clr(Reset));  // open: load, D, carry

  // Other names for the same wires on the sheet: func[5:0] = IM[5:0]; instr_index[25:0] = IM[25:0];
  //   operate[5:0] = IM[31:26]; 无条件分支指令数[15:0] = unconditional; 有条件分支成功跳转[15:0] = conditionalsucces;
  //   有条件分支指令数[15:0] = conditional
endmodule

module IF_ID (
  input  [31:0] Insin,
  input  [31:0] PCin,
  input  clk,
  input  rst,
  input  in_5,
  output [31:0] Insout,
  output [31:0] PCout
);

  wire not_1_out;

  not not_1 (not_1_out, in_5);
  Register #(.width(32)) register_1 (.D(Insin), .en(not_1_out), .Q(Insout), .clk(clk), .clr(rst));
  Register #(.width(32)) register_2 (.D(PCin), .en(not_1_out), .Q(PCout), .clk(clk), .clr(rst));
endmodule

module ID_EX (
  input  LWin,
  input  [31:0] RAin,
  input  JALin,
  input  [31:0] RBin,
  input  [4:0] RDin,
  input  _16ExtImmin,
  input  [4:0] RTin,
  input  SextImmin,
  input  WEin,
  input  _5extImmin,
  input  [31:0] OFFSETin,
  input  SWin,
  input  [4:0] RAin_2,
  input  [3:0] ALUOPin,
  input  [4:0] RBin_2,
  input  [31:0] PCin,
  input  SYSin,
  input  halt,
  input  clk,
  input  rst,
  output LWout,
  output [31:0] RAout,
  output JALout,
  output [31:0] RBout,
  output [4:0] RDout,
  output _16ExtImmout,
  output [4:0] RTout,
  output SextImmout,
  output WEout,
  output _5extImmout,
  output [31:0] OFFsetout,
  output SWout,
  output [4:0] RAout_2,
  output [3:0] ALUOPout,
  output [4:0] RBout_2,
  output [31:0] PCout,
  output SYSout
);

  wire not_1_out;

  not not_1 (not_1_out, halt);
  Register #(.width(32)) register_1 (.D(RAin), .en(not_1_out), .Q(RAout), .clk(clk), .clr(rst));
  Register #(.width(32)) register_2 (.D(RBin), .en(not_1_out), .Q(RBout), .clk(clk), .clr(rst));
  Register #(.width(1)) register_3 (.D(_16ExtImmin), .en(not_1_out), .Q(_16ExtImmout), .clk(clk), .clr(rst));
  Register #(.width(1)) register_4 (.D(SextImmin), .en(not_1_out), .Q(SextImmout), .clk(clk), .clr(rst));
  Register #(.width(1)) register_5 (.D(_5extImmin), .en(not_1_out), .Q(_5extImmout), .clk(clk), .clr(rst));
  Register #(.width(1)) register_6 (.D(SWin), .en(not_1_out), .Q(SWout), .clk(clk), .clr(rst));
  Register #(.width(4)) register_7 (.D(ALUOPin), .en(not_1_out), .Q(ALUOPout), .clk(clk), .clr(rst));
  Register #(.width(32)) register_8 (.D(PCin), .en(not_1_out), .Q(PCout), .clk(clk), .clr(rst));
  Register #(.width(1)) register_9 (.D(SYSin), .en(not_1_out), .Q(SYSout), .clk(clk), .clr(rst));
  Register #(.width(1)) register_10 (.D(LWin), .en(not_1_out), .Q(LWout), .clk(clk), .clr(rst));
  Register #(.width(1)) register_11 (.D(JALin), .en(not_1_out), .Q(JALout), .clk(clk), .clr(rst));
  Register #(.width(5)) register_12 (.D(RDin), .en(not_1_out), .Q(RDout), .clk(clk), .clr(rst));
  Register #(.width(5)) register_13 (.D(RTin), .en(not_1_out), .Q(RTout), .clk(clk), .clr(rst));
  Register #(.width(1)) register_14 (.D(WEin), .en(not_1_out), .Q(WEout), .clk(clk), .clr(rst));
  Register #(.width(32)) register_15 (.D(OFFSETin), .en(not_1_out), .Q(OFFsetout), .clk(clk), .clr(rst));
  Register #(.width(5)) register_16 (.D(RAin_2), .en(not_1_out), .Q(RAout_2), .clk(clk), .clr(rst));
  Register #(.width(5)) register_17 (.D(RBin_2), .en(not_1_out), .Q(RBout_2), .clk(clk), .clr(rst));
endmodule

module EX_MEM (
  input  LWin,
  input  [31:0] Rin,
  input  JALin,
  input  [31:0] RBin,
  input  [4:0] RDin,
  input  _16ExtImmin,
  input  [4:0] RTin,
  input  SextImmin,
  input  WEin,
  input  _5extImmin,
  input  [4:0] RAin,
  input  SWin,
  input  [4:0] RBin_2,
  input  [3:0] ALUOPin,
  input  SYSin,
  input  [31:0] PCin,
  input  clk,
  input  rst,
  input  halt,
  output LWout,
  output [31:0] Rout,
  output JALout,
  output [31:0] RBout,
  output [4:0] RDout,
  output _16ExtImmout,
  output [4:0] RTout,
  output SextImmout,
  output WEout,
  output _5extImmout,
  output [4:0] RAout,
  output SWout,
  output [4:0] RBout_2,
  output [3:0] ALUOPout,
  output SYSout,
  output [31:0] PCout
);

  wire not_1_out;

  not not_1 (not_1_out, halt);
  Register #(.width(32)) register_1 (.D(Rin), .en(not_1_out), .Q(Rout), .clk(clk), .clr(rst));
  Register #(.width(32)) register_2 (.D(RBin), .en(not_1_out), .Q(RBout), .clk(clk), .clr(rst));
  Register #(.width(1)) register_3 (.D(_16ExtImmin), .en(not_1_out), .Q(_16ExtImmout), .clk(clk), .clr(rst));
  Register #(.width(1)) register_4 (.D(SextImmin), .en(not_1_out), .Q(SextImmout), .clk(clk), .clr(rst));
  Register #(.width(1)) register_5 (.D(_5extImmin), .en(not_1_out), .Q(_5extImmout), .clk(clk), .clr(rst));
  Register #(.width(1)) register_6 (.D(SWin), .en(not_1_out), .Q(SWout), .clk(clk), .clr(rst));
  Register #(.width(4)) register_7 (.D(ALUOPin), .en(not_1_out), .Q(ALUOPout), .clk(clk), .clr(rst));
  Register #(.width(32)) register_8 (.D(PCin), .en(not_1_out), .Q(PCout), .clk(clk), .clr(rst));
  Register #(.width(1)) register_9 (.D(LWin), .en(not_1_out), .Q(LWout), .clk(clk), .clr(rst));
  Register #(.width(1)) register_10 (.D(JALin), .en(not_1_out), .Q(JALout), .clk(clk), .clr(rst));
  Register #(.width(5)) register_11 (.D(RDin), .en(not_1_out), .Q(RDout), .clk(clk), .clr(rst));
  Register #(.width(5)) register_12 (.D(RTin), .en(not_1_out), .Q(RTout), .clk(clk), .clr(rst));
  Register #(.width(1)) register_13 (.D(WEin), .en(not_1_out), .Q(WEout), .clk(clk), .clr(rst));
  Register #(.width(5)) register_14 (.D(RAin), .en(not_1_out), .Q(RAout), .clk(clk), .clr(rst));
  Register #(.width(5)) register_15 (.D(RBin_2), .en(not_1_out), .Q(RBout_2), .clk(clk), .clr(rst));
  Register #(.width(1)) register_16 (.D(SYSin), .en(not_1_out), .Q(SYSout), .clk(clk), .clr(rst));
endmodule

module MEM_WB (
  input  [31:0] Rin,
  input  WEin,
  input  [31:0] DATAin,
  input  [4:0] RDin,
  input  [4:0] RTin,
  input  [31:0] PCin,
  input  LWin,
  input  _16ExtImmin,
  input  JALin,
  input  SextImmin,
  input  SYSin,
  input  [4:0] RAin,
  input  [4:0] RBin,
  input  clk,
  input  rst,
  input  halt,
  output WEout,
  output [31:0] Wout,
  output [4:0] rWin,
  output SYSout,
  output [4:0] RAout,
  output [4:0] RBout
);

  wire not_1_out, register_11_q, register_12_q;
  wire [0:0] register_6_q;
  wire [1:0] or_1_out;
  wire [4:0] register_9_q, register_10_q;
  wire [31:0] adder_1_out, register_3_q, register_4_q, register_5_q;

  not not_1 (not_1_out, halt);
  Adder #(.width(32)) adder_1 (.a(PCin), .b(32'h4), .out(adder_1_out));  // open: cin, cout
  Register #(.width(5)) register_1 (.D(RAin), .en(not_1_out), .Q(RAout), .clk(clk), .clr(rst));
  Register #(.width(5)) register_2 (.D(RBin), .en(not_1_out), .Q(RBout), .clk(clk), .clr(rst));
  Register #(.width(32)) register_3 (.D(Rin), .en(not_1_out), .Q(register_3_q), .clk(clk), .clr(rst));
  Register #(.width(32)) register_4 (.D(DATAin), .en(not_1_out), .Q(register_4_q), .clk(clk), .clr(rst));
  Register #(.width(32)) register_5 (.D(adder_1_out), .en(not_1_out), .Q(register_5_q), .clk(clk), .clr(rst));
  Register #(.width(1)) register_6 (.D(LWin), .en(not_1_out), .Q(register_6_q[0]), .clk(clk), .clr(rst));
  Register #(.width(1)) register_7 (.D(JALin), .en(not_1_out), .Q(or_1_out[1]), .clk(clk), .clr(rst));
  Multiplexer #(.select(2), .width(32), .disabled(0), .enable("false")) multiplexer_1 (
    .in0(register_3_q), .in1(register_4_q), .in2(register_5_q), .in3({32{1'b0}}), .out(Wout),
    .sel({or_1_out[1], register_6_q[0]}));
  Register #(.width(1)) register_8 (.D(WEin), .en(not_1_out), .Q(WEout), .clk(clk), .clr(rst));
  Register #(.width(5)) register_9 (.D(RDin), .en(not_1_out), .Q(register_9_q), .clk(clk), .clr(rst));
  Register #(.width(5)) register_10 (.D(RTin), .en(not_1_out), .Q(register_10_q), .clk(clk), .clr(rst));
  Register #(.width(1)) register_11 (.D(_16ExtImmin), .en(not_1_out), .Q(register_11_q), .clk(clk), .clr(rst));
  Register #(.width(1)) register_12 (.D(SextImmin), .en(not_1_out), .Q(register_12_q), .clk(clk), .clr(rst));
  Register #(.width(1)) register_13 (.D(SYSin), .en(not_1_out), .Q(SYSout), .clk(clk), .clr(rst));
  Multiplexer #(.select(2), .width(5), .disabled(0), .enable("false")) multiplexer_2 (
    .in0(register_9_q), .in1(register_10_q), .in2({5{1'b1}}), .in3({5{1'b0}}), .out(rWin), .sel(or_1_out));
  or or_1 (or_1_out[0], register_11_q, register_12_q);
endmodule
