// Logisim project cpu_benchmark.circ as structural Verilog: 9 circuits, main circuit cpu
module cpu (
  input  in_1
);

  wire _5ExtImm, and_1_out, and_2_out, BEQ, BNE, choice, clock_1_out, comparator_1_eq, controler_1__16extimm,
       controler_1_beq, controler_1_bne, controler_1_j, controler_1_jal, controler_1_jr, controler_1_lw,
       controler_1_regwrite, controler_1_sextimm, controler_1_sw, controler_1_syscall, ex_mem_1_jalout,
       ex_mem_1_lwout, ex_mem_1_swout, ex_mem_1_sysout, Go, halt, id_ex_1__5extimmout, id_ex_1__16extimmout,
       id_ex_1_lwout, id_ex_1_sextimmout, id_ex_1_swout, id_ex_1_sysout, IR1, IR2, IR3, J, JAL, JR,
       not_1_out, not_2_out, not_3_out, not_4_out, not_5_out, or_1_out, or_3_out, registerfile_1_p3, RST, SH,
       stall, stop, syscall, W1, W2, W3, WE1, WE2;
  wire [1:0] SRC;
  wire [3:0] controler_1_aluop, id_ex_1_aluopout;
  wire [4:0] DES1, DES2, rA_t, rB_t, registerfile_1_p4, Rs, Rt;
  wire [11:0] EX_PC, ID_PC, IF_PC, WB_PC;
  wire [15:0] counter_1_q, if_id_1_insout_2, \load_use次数 , \总周期数 , \插入气泡数 , \无条件分支指令数 , \有条件分支成功跳转 ;
  wire [25:0] id_ex_1_indexout;
  wire [31:0] adder_2_out, alu_1_result, bit_extender_1_out, bit_extender_2_out, branch_1_nextpc,
       ex_mem_1_pcout, ex_mem_1_rbout, ex_mem_1_rout, id_ex_1_offsetout, id_ex_1_pcout, id_ex_1_raout,
       id_ex_1_rbout, if_id_1_pcout, multiplexer_1_out, multiplexer_4_out, multiplexer_5_out,
       multiplexer_6_out, PC_q, RA, ram_1_data, RB, registerfile_1_p1, rom_1_data, SyscallOut;
  wire [31:26] if_id_1_insout;

  Button \u_总复位  (.out(RST));
  Button _1 (.out(IR1));
  Button _2 (.out(IR2));
  Button _3 (.out(IR3));
  Button \u_继续运行  (.out(Go));
  LED led_1 (.in(W1));
  LED led_2 (.in(W2));
  LED led_3 (.in(W3));
  // Probe on IF_PC
  not not_1 (not_1_out, or_1_out);
  or or_1 (or_1_out, stall, halt);
  Clock clock_1 (.out(clock_1_out));
  not not_2 (not_2_out, halt);
  and and_1 (and_1_out, syscall, not_3_out);
  Hex_Digit_Display hex_digit_display_1 (.value(SyscallOut[31:28]));  // open: dp
  Register #(.width(32)) a0 (.D(RB), .en(and_1_out), .Q(SyscallOut), .clk(clock_1_out), .clr(RST));
  not not_3 (not_3_out, halt);
  Hex_Digit_Display hex_digit_display_2 (.value(SyscallOut[23:20]));  // open: dp
  Hex_Digit_Display hex_digit_display_3 (.value(SyscallOut[27:24]));  // open: dp
  // Probe on ID_PC
  Counter #(.width(16), .max('hffff)) counter_1 (
    .count(not_2_out), .Q(counter_1_q), .clk(clock_1_out), .clr(RST));  // open: load, D, carry
  Hex_Digit_Display hex_digit_display_4 (.value(SyscallOut[19:16]));  // open: dp
  Hex_Digit_Display hex_digit_display_5 (.value(SyscallOut[15:12]));  // open: dp
  // Probe on adder_2_out
  // Probe on branch_1_nextpc
  Hex_Digit_Display hex_digit_display_6 (.value(SyscallOut[11:8]));  // open: dp
  Hex_Digit_Display hex_digit_display_7 (.value(SyscallOut[7:4]));  // open: dp
  // Probe on EX_PC
  Multiplexer #(.width(32), .enable("false")) multiplexer_1 (
    .in0(adder_2_out), .in1(branch_1_nextpc), .out(multiplexer_1_out), .sel(choice));
  Adder #(.width(16)) adder_1 (.a(counter_1_q), .b({{15{1'b0}}, halt}), .out(\总周期数 ));  // open: cin, cout
  Comparator #(.width(32)) comparator_1 (.a(32'h22), .b(RA), .eq(comparator_1_eq));  // open: gt, lt
  not not_4 (not_4_out, comparator_1_eq);
  Hex_Digit_Display hex_digit_display_8 (.value(SyscallOut[3:0]));  // open: dp
  // Probe on EX_PC
  Adder #(.width(32)) adder_2 (.a(32'h4), .b(PC_q), .out(adder_2_out));  // open: cin, cout
  Register #(.width(32)) PC (.D(multiplexer_1_out), .en(not_1_out), .Q(PC_q), .clk(clock_1_out), .clr(RST));
  and and_2 (and_2_out, not_4_out, syscall);
  Multiplexer #(.width(5), .enable("false")) multiplexer_2 (.in0(Rs), .in1(5'b00010), .out(rA_t), .sel(syscall));
  not not_5 (not_5_out, in_1);
  and and_3 (halt, not_5_out, and_2_out);
  // Probe on \总周期数 
  // Probe on \无条件分支指令数 
  // Probe on \有条件分支成功跳转 
  // Probe on \load_use次数 
  // Probe on \插入气泡数 
  // Probe on WB_PC
  ROM #(.addrWidth(10), .dataWidth(32)) rom_1 (.addr(PC_q[11:2]), .data(rom_1_data));  // open: sel
  Multiplexer #(.width(5), .enable("false")) multiplexer_3 (.in0(Rt), .in1(5'b00100), .out(rB_t), .sel(syscall));
  IF_ID if_id_1 (
    .Insin(rom_1_data), .PCin(PC_q), .clk(clock_1_out), .Insout({if_id_1_insout, Rs, Rt, if_id_1_insout_2}),
    .PCout(if_id_1_pcout), .rst(choice), .halt(stall));
  controler controler_1 (
    .operator(if_id_1_insout), .func(if_id_1_insout_2[5:0]), .AluOp(controler_1_aluop), .LW(controler_1_lw),
    ._16ExtImm(controler_1__16extimm), .JAL(controler_1_jal), .syscall(controler_1_syscall),
    .SW(controler_1_sw), .SExtImm(controler_1_sextimm), ._5ExtImm(_5ExtImm), .SH(SH),
    .RegWrite(controler_1_regwrite), .SRC(SRC), .BNE(controler_1_bne), .BEQ(controler_1_beq),
    .J(controler_1_j), .JR(controler_1_jr));
  Handler handler_1 (
    .DES1(DES1), .RS(Rs), .WE1(WE1), .DES2(DES2), .RT(Rt), .WE2(WE2), .Result(stall), .SRC(SRC),
    .syscall(controler_1_syscall), .jal(controler_1_jal));
  assign bit_extender_1_out = {{16{if_id_1_insout_2[15]}}, if_id_1_insout_2};  // Bit_Extender bit_extender_1
  assign bit_extender_2_out = {{27{1'b0}}, if_id_1_insout_2[10:6]};  // Bit_Extender bit_extender_2
  Multiplexer #(.width(32), .enable("false")) multiplexer_4 (
    .in0(bit_extender_1_out), .in1(bit_extender_2_out), .out(multiplexer_4_out), .sel(_5ExtImm));
  // RegisterFile registerfile_1: pin names not known; wires that end beside it: registerfile_1_p1, clock_1_out, registerfile_1_p3, registerfile_1_p4, rA_t, rB_t, RA, RB
  or or_2 (stop, choice, stall);
  ID_EX id_ex_1 (
    .LWin(controler_1_lw), .LWout(id_ex_1_lwout), .RAin(RA), .RAout(id_ex_1_raout), .JALin(controler_1_jal),
    .JALout(JAL), .RBin(RB), .RBout(id_ex_1_rbout), .RDin(if_id_1_insout_2[15:11]),
    ._16ExtImmin(controler_1__16extimm), .RTin(Rt), .SextImmin(controler_1_sextimm),
    .WEin(controler_1_regwrite), .WEout(WE1), ._5extImmin(_5ExtImm), ._5extImmout(id_ex_1__5extimmout),
    .OFFSETin(multiplexer_4_out), .OFFsetout(id_ex_1_offsetout), .SWin(controler_1_sw),
    .SWout(id_ex_1_swout), .ALUOPin(controler_1_aluop), .ALUOPout(id_ex_1_aluopout), .PCin(if_id_1_pcout),
    .PCout(id_ex_1_pcout), .SYSin(controler_1_syscall), .SYSout(id_ex_1_sysout), .halt(halt),
    .clk(clock_1_out), .rst(stop), .DESout(DES1), .SextImmout(id_ex_1_sextimmout),
    ._16ExtImmout(id_ex_1__16extimmout), .INDEXin({Rs, Rt, if_id_1_insout_2}), .INDEXout(id_ex_1_indexout),
    .BEQ(controler_1_beq), .BEQ_2(BEQ), .BNE(controler_1_bne), .BNE_2(BNE), .JR(controler_1_jr), .JR_2(JR),
    .J(controler_1_j), .J_2(J));
  Multiplexer #(.width(32), .enable("false")) multiplexer_5 (
    .in0(id_ex_1_raout), .in1(id_ex_1_rbout), .out(multiplexer_5_out), .sel(id_ex_1__5extimmout));
  Branch branch_1 (
    .PC(id_ex_1_pcout), .OFFSET(id_ex_1_offsetout), .ins_index(id_ex_1_indexout), .RA(id_ex_1_raout),
    .RB(id_ex_1_rbout), .BNE(BNE), .BEQ(BEQ), .NextPC(branch_1_nextpc), .JR(JR), .J(J), .JAL(JAL),
    .choice(choice));
  Multiplexer #(.width(32), .enable("false")) multiplexer_6 (
    .in0(id_ex_1_rbout), .in1(id_ex_1_offsetout), .out(multiplexer_6_out), .sel(or_3_out));
  or or_3 (or_3_out, id_ex_1__16extimmout, id_ex_1_sextimmout, id_ex_1__5extimmout);
  ALU alu_1 (
    .AluOP(id_ex_1_aluopout), .X(multiplexer_5_out), .Result(alu_1_result), .Y(multiplexer_6_out));  // open: Equal, Signed_Overflow, Result_2, UnSigned_Overflow
  EX_MEM ex_mem_1 (
    .LWin(id_ex_1_lwout), .LWout(ex_mem_1_lwout), .Rin(alu_1_result), .Rout(ex_mem_1_rout), .JALin(JAL),
    .JALout(ex_mem_1_jalout), .RBin(id_ex_1_rbout), .RBout(ex_mem_1_rbout), .SWin(id_ex_1_swout),
    .SWout(ex_mem_1_swout), .PCin(id_ex_1_pcout), .PCout(ex_mem_1_pcout), .clk(clock_1_out), .WEin(WE1),
    .WEout(WE2), .rst(RST), .halt(halt), .SYSin(id_ex_1_sysout), .SYSout(ex_mem_1_sysout), .DESin(DES1),
    .DESout(DES2));
  RAM #(.addrWidth(12), .dataWidth(32), .bus("separate")) ram_1 (
    .addr(ex_mem_1_rout[13:2]), .din(ex_mem_1_rbout), .data(ram_1_data), .str(ex_mem_1_swout), .sel(1'b1),
    .clk(clock_1_out), .ld(1'b1), .clr(RST));
  MEM_WB mem_wb_1 (
    .Rin(ex_mem_1_rout), .DATAin(ram_1_data), .clk(clock_1_out), .PCin(ex_mem_1_pcout),
    .Wout(registerfile_1_p1), .LWin(ex_mem_1_lwout), .JALin(ex_mem_1_jalout), .WEin(WE2),
    .WEout(registerfile_1_p3), .rst(RST), .halt(halt), .SYSout(syscall), .SYSin(ex_mem_1_sysout),
    .DESin(DES2), .rWin(registerfile_1_p4));

  // Notes on the sheet:
  //   中断源
  //   中断请求指示
  //   数码管输出应该用寄存器锁存，否则显示数据只能一闪而过
  //   可以通过项目增加Logisim库的方式将前几次实验完成的电路作为子电路引入到本电路中使用
  //   数码管输出
  //   总复位信号应将除ROM以外所有存储组件全部清零
  //   指令存储器
  //   contents of rom_1 (hex, n*v repeats v):
  //   20110001 8000c05 20110001 20120002 20130003 8000c09 20110001 20120002 20130003 8000c0d 20110001
  //   20120002 20130003 8000c11 20110001 20120002 20130003 c000cb8 20100001 20110001 118fc0 112020
  //   20020022 c 118882 12200001 8000c15 112020 20020022 c 20110001 118880 112020 20020022 c 12200001
  //   8000c1f 20110001 118fc0 112020 20020022 c 1188c3 112020 20020022 c 118903 112020 20020022 c 118903
  //   112020 20020022 c 118903 112020 20020022 c 118903 112020 20020022 c 118903 112020 20020022 c 118903
  //   112020 20020022 c 118903 112020 20020022 c 20100001 109fc0 139fc3 8021 2012000c 24160003 26100001
  //   3210000f 20080008 20090001 139900 2709825 132020 20020022 c 1094022 1500fff9 22100001 2018000f
  //   2188024 108700 20080008 20090001 139902 2709825 132021 20020022 c 1094022 1500fff9 108702 2c9b022
  //   12c00001 8000c50 4020 1084027 84400 3508ffff 82021 20020022 c 2010ffff 20110000 ae300000 22100001
  //   22310004 ae300000 22100001 22310004 ae300000 22100001 22310004 ae300000 22100001 22310004 ae300000
  //   22100001 22310004 ae300000 22100001 22310004 ae300000 22100001 22310004 ae300000 22100001 22310004
  //   ae300000 22100001 22310004 ae300000 22100001 22310004 ae300000 22100001 22310004 ae300000 22100001
  //   22310004 ae300000 22100001 22310004 ae300000 22100001 22310004 ae300000 22100001 22310004 ae300000
  //   22100001 22310004 22100001 8020 2011003c 8e130000 8e340000 274402a 11000002 ae330000 ae140000
  //   2231fffc 1611fff8 102020 20020022 c 22100004 2011003c 1611fff2 2002000a c 20100000 22100001 102020
  //   20020022 c 22100002 102020 20020022 c 22100003 102020 20020022 c 22100004 102020 20020022 c 22100005
  //   102020 20020022 c 22100006 102020 20020022 c 22100007 102020 20020022 c 22100008 102020 20020022
  //   20020022 c 3e00008
  //   寄存器文件
endmodule

module controler (
  input  [5:0] operator,
  input  [5:0] func,
  output syscall,
  output _16ExtImm,
  output SExtImm,
  output _5ExtImm,
  output BNE,
  output J,
  output [3:0] AluOp,
  output LW,
  output SW,
  output SH,
  output BEQ,
  output JR,
  output RegWrite,
  output JAL,
  output [1:0] SRC
);

  wire ADD, ADDI, ADDIU, ADDU, AND, ANDI, BGTZ, comparator_15_eq, comparator_16_eq, comparator_17_eq,
       comparator_18_eq, comparator_19_eq, comparator_20_eq, comparator_21_eq, comparator_22_eq,
       comparator_23_eq, comparator_24_eq, comparator_25_eq, comparator_26_eq, comparator_27_eq,
       comparator_28_eq, comparator_29_eq, NOR, OR, ORI, R1, SLL, SLLV, sllv_srlv, SLT, SLTI, SLTU, SRA, SRL,
       SRLV, SUB;
  wire [1:0] or_8_out;
  wire [3:0] and_16_out, and_17_out, and_18_out, and_19_out, and_20_out, and_21_out, and_22_out, and_23_out,
       and_24_out, and_25_out;
  wire [3:3] or_1_out, or_2_out, or_3_out, or_4_out, or_5_out, or_6_out;

  Comparator #(.width(6)) comparator_1 (.a(operator), .b({6{1'b0}}), .eq(R1));  // open: gt, lt
  Comparator #(.width(6)) comparator_2 (.a(operator), .b(6'b000010), .eq(J));  // open: gt, lt
  Comparator #(.width(6)) comparator_3 (.a(operator), .b(6'b000011), .eq(JAL));  // open: gt, lt
  Comparator #(.width(6)) comparator_4 (.a(operator), .b(6'b000100), .eq(BEQ));  // open: gt, lt
  Comparator #(.width(6)) comparator_5 (.a(operator), .b(6'b000101), .eq(BNE));  // open: gt, lt
  Comparator #(.width(6)) comparator_6 (.a(operator), .b(6'b000111), .eq(BGTZ));  // open: gt, lt
  Comparator #(.width(6)) comparator_7 (.a(operator), .b(6'b001000), .eq(ADDI));  // open: gt, lt
  Comparator #(.width(6)) comparator_8 (.a(operator), .b(6'b001001), .eq(ADDIU));  // open: gt, lt
  Comparator #(.width(6)) comparator_9 (.a(operator), .b(6'b001010), .eq(SLTI));  // open: gt, lt
  Comparator #(.width(6)) comparator_10 (.a(operator), .b(6'b001100), .eq(ANDI));  // open: gt, lt
  Comparator #(.width(6)) comparator_11 (.a(operator), .b(6'b001101), .eq(ORI));  // open: gt, lt
  Comparator #(.width(6)) comparator_12 (.a(operator), .b(6'b100011), .eq(LW));  // open: gt, lt
  Comparator #(.width(6)) comparator_13 (.a(operator), .b(6'b101001), .eq(SH));  // open: gt, lt
  Comparator #(.width(6)) comparator_14 (.a(operator), .b(6'b101011), .eq(SW));  // open: gt, lt
  Comparator #(.width(6)) comparator_15 (.a(func), .b({6{1'b0}}), .eq(comparator_15_eq));  // open: gt, lt
  Comparator #(.width(6)) comparator_16 (.a(func), .b(6'b000010), .eq(comparator_16_eq));  // open: gt, lt
  Comparator #(.width(6)) comparator_17 (.a(func), .b(6'b000011), .eq(comparator_17_eq));  // open: gt, lt
  Comparator #(.width(6)) comparator_18 (.a(func), .b(6'b000100), .eq(comparator_18_eq));  // open: gt, lt
  Comparator #(.width(6)) comparator_19 (.a(func), .b(6'b000110), .eq(comparator_19_eq));  // open: gt, lt
  Comparator #(.width(6)) comparator_20 (.a(func), .b(6'b001000), .eq(comparator_20_eq));  // open: gt, lt
  Comparator #(.width(6)) comparator_21 (.a(func), .b(6'b001100), .eq(comparator_21_eq));  // open: gt, lt
  Comparator #(.width(6)) comparator_22 (.a(func), .b(6'b100000), .eq(comparator_22_eq));  // open: gt, lt
  Comparator #(.width(6)) comparator_23 (.a(func), .b(6'b100001), .eq(comparator_23_eq));  // open: gt, lt
  Comparator #(.width(6)) comparator_24 (.a(func), .b(6'b100010), .eq(comparator_24_eq));  // open: gt, lt
  Comparator #(.width(6)) comparator_25 (.a(func), .b(6'b100100), .eq(comparator_25_eq));  // open: gt, lt
  Comparator #(.width(6)) comparator_26 (.a(func), .b(6'b100101), .eq(comparator_26_eq));  // open: gt, lt
  Comparator #(.width(6)) comparator_27 (.a(func), .b(6'b100111), .eq(comparator_27_eq));  // open: gt, lt
  Comparator #(.width(6)) comparator_28 (.a(func), .b(6'b101010), .eq(comparator_28_eq));  // open: gt, lt
  Comparator #(.width(6)) comparator_29 (.a(func), .b(6'b101011), .eq(comparator_29_eq));  // open: gt, lt
  and and_1 (SLL, R1, comparator_15_eq);
  and and_2 (SRL, R1, comparator_16_eq);
  and and_3 (SRA, R1, comparator_17_eq);
  and and_4 (SLLV, R1, comparator_18_eq);
  and and_5 (SRLV, R1, comparator_19_eq);
  and and_6 (JR, R1, comparator_20_eq);
  and and_7 (syscall, R1, comparator_21_eq);
  and and_8 (ADD, R1, comparator_22_eq);
  and and_9 (ADDU, R1, comparator_23_eq);
  and and_10 (SUB, R1, comparator_24_eq);
  and and_11 (AND, R1, comparator_25_eq);
  and and_12 (OR, R1, comparator_26_eq);
  and and_13 (NOR, R1, comparator_27_eq);
  and and_14 (SLT, R1, comparator_28_eq);
  and and_15 (SLTU, R1, comparator_29_eq);
  or or_1 (or_1_out[3], ADD, ADDI, ADDU, ADDIU, SW, LW, SH);
  or or_2 (or_2_out[3], AND, ANDI);
  or or_3 (or_3_out[3], OR, ORI);
  or or_4 (or_4_out[3], SLL, SLLV);
  or or_5 (or_5_out[3], SLT, SLTI);
  or or_6 (or_6_out[3], SRL, SRLV);
  assign and_16_out = 4'b0101 & {4{or_1_out[3]}};  // AND_Gate and_16, 4 bits wide
  assign and_17_out = 4'b0111 & {4{or_2_out[3]}};  // AND_Gate and_17, 4 bits wide
  assign and_18_out = 4'b1000 & {4{or_3_out[3]}};  // AND_Gate and_18, 4 bits wide
  assign and_19_out = 4'b0000 & {4{or_4_out[3]}};  // AND_Gate and_19, 4 bits wide
  assign and_20_out = 4'b1010 & {4{NOR}};  // AND_Gate and_20, 4 bits wide
  assign and_21_out = 4'b0001 & {4{SRA}};  // AND_Gate and_21, 4 bits wide
  assign and_22_out = 4'b1011 & {4{or_5_out[3]}};  // AND_Gate and_22, 4 bits wide
  assign and_23_out = 4'b1100 & {4{SLTU}};  // AND_Gate and_23, 4 bits wide
  assign and_24_out = 4'b0110 & {4{SUB}};  // AND_Gate and_24, 4 bits wide
  assign and_25_out = 4'b0010 & {4{or_6_out[3]}};  // AND_Gate and_25, 4 bits wide
  assign AluOp = and_16_out | and_17_out | and_18_out | and_19_out | and_20_out | and_21_out | and_22_out | and_23_out | and_24_out | and_25_out;  // OR_Gate or_7, 4 bits wide
  or or_8 (or_8_out[0], SLL, SH, R1, SW, BEQ, BNE, SRL, SRA);
  or or_9 (or_8_out[1], ANDI, ADDIU, ADDI, R1, SW, SH, BNE, BEQ, ORI, LW, SLTI);
  or or_10 (_16ExtImm, ANDI, ORI);
  or or_11 (SExtImm, ADDI, ADDIU, LW, SW, SH, BNE, BGTZ, BEQ, SLTI);
  or or_12 (_5ExtImm, SLL, SRA, SRL);
  or or_13 (sllv_srlv, SRLV, SLLV);
  Multiplexer #(.width(2), .enable("false")) multiplexer_1 (.in0(or_8_out), .in1(2'b10), .out(SRC), .sel(JR));
  or or_14 (RegWrite, SRLV, ADD, ADDU, ADDI, ADDIU, AND, ANDI, SLL, SLLV, SRL, SRA, OR, ORI, NOR, SLT, SLTU, SLTI, SUB, JAL, LW);

  // Other names for the same wires on the sheet: operate[5:0] = operator
endmodule

module NPC (
  input  Reset,
  input  CLK,
  input  [31:0] IM,
  input  [31:0] PC,
  input  [31:0] RegRS,
  input  [31:0] RegRT,
  input  [31:0] OFFSET,
  output [31:0] NextPC,
  output [15:0] unconditional,
  output [15:0] conditional,
  output [15:0] conditionalsucces
);

  wire and_3_out, and_4_out, and_5_out, BEQ, BGTZ, BNE, comparator_1_eq, comparator_2_eq, comparator_3_eq,
       comparator_4_eq, comparator_4_gt, comparator_10_eq, halt, J, JAL, JR, not_1_out, not_2_out, or_3_out,
       or_4_out, syscall;
  wire [1:0] or_2_out;
  wire [31:0] adder_1_out, adder_2_out, multiplexer_1_out, multiplexer_2_out;

  Multiplexer #(.width(32), .enable("false")) multiplexer_1 (
    .in0(RegRT), .in1({32{1'b0}}), .out(multiplexer_1_out), .sel(BGTZ));
  // Probe on PC
  Comparator #(.width(6)) comparator_1 (.a(IM[5:0]), .b(6'b001000), .eq(comparator_1_eq));  // open: gt, lt
  Comparator #(.width(6)) comparator_2 (.a(IM[31:26]), .b({6{1'b0}}), .eq(comparator_2_eq));  // open: gt, lt
  Comparator #(.width(6)) comparator_3 (.a(IM[5:0]), .b(6'b001100), .eq(comparator_3_eq));  // open: gt, lt
  Adder #(.width(32)) adder_1 (.a(PC), .b(32'h4), .out(adder_1_out));  // open: cin, cout
  Multiplexer #(.width(32), .enable("false")) multiplexer_2 (
    .in0({PC[31:28], IM[25:0], 2'b00}), .in1(RegRS), .out(multiplexer_2_out), .sel(JR));
  Adder #(.width(32)) adder_2 (.a({OFFSET[29:0], 2'b00}), .b(adder_1_out), .out(adder_2_out));  // open: cin, cout
  Comparator #(.width(32)) comparator_4 (
    .a(RegRS), .b(multiplexer_1_out), .gt(comparator_4_gt), .eq(comparator_4_eq));  // open: lt
  Comparator #(.width(6)) comparator_5 (.a(IM[31:26]), .b(6'b000010), .eq(J));  // open: gt, lt
  Comparator #(.width(6)) comparator_6 (.a(IM[31:26]), .b(6'b000011), .eq(JAL));  // open: gt, lt
  and and_1 (JR, comparator_1_eq, comparator_2_eq);
  and and_2 (syscall, comparator_2_eq, comparator_3_eq);
  not not_1 (not_1_out, comparator_4_eq);
  and and_3 (and_3_out, BGTZ, comparator_4_gt);
  and and_4 (and_4_out, not_1_out, BNE);
  and and_5 (and_5_out, comparator_4_eq, BEQ);
  Multiplexer #(.select(2), .width(32)) multiplexer_3 (
    .in0(adder_1_out), .in1(adder_2_out), .in2(multiplexer_2_out), .out(NextPC), .sel(or_2_out),
    .en(not_2_out));  // open: in3
  or or_1 (or_2_out[1], J, JAL, JR);
  or or_2 (or_2_out[0], and_3_out, and_4_out, and_5_out);
  Comparator #(.width(6)) comparator_7 (.a(IM[31:26]), .b(6'b000101), .eq(BNE));  // open: gt, lt
  Comparator #(.width(6)) comparator_8 (.a(IM[31:26]), .b(6'b000111), .eq(BGTZ));  // open: gt, lt
  Comparator #(.width(6)) comparator_9 (.a(IM[31:26]), .b(6'b000100), .eq(BEQ));  // open: gt, lt
  Comparator #(.width(32)) comparator_10 (.a(RegRS), .b(32'ha), .eq(comparator_10_eq));  // open: gt, lt
  not not_2 (not_2_out, Reset);
  and and_6 (halt, comparator_10_eq, syscall);
  or or_3 (or_3_out, J, JAL, JR);
  or or_4 (or_4_out, BNE, BGTZ, BEQ);
  Counter #(.width(16), .max('hffff)) counter_1 (
    .count(or_3_out), .Q(unconditional), .clk(CLK), .clr(Reset));  // open: load, D, carry
  Counter #(.width(16), .max('hffff)) counter_2 (
    .count(or_4_out), .Q(conditional), .clk(CLK), .clr(Reset));  // open: load, D, carry
  Counter #(.width(16), .max('hffff)) counter_3 (
    .count(or_2_out[0]), .Q(conditionalsucces), .clk(CLK), .clr(Reset));  // open: load, D, carry

  // Other names for the same wires on the sheet: func[5:0] = IM[5:0]; instr_index[25:0] = IM[25:0];
  //   operate[5:0] = IM[31:26]; 无条件分支指令数[15:0] = unconditional; 有条件分支成功跳转[15:0] = conditionalsucces;
  //   有条件分支指令数[15:0] = conditional
endmodule

module IF_ID (
  input  [31:0] Insin,
  input  [31:0] PCin,
  input  clk,
  input  rst,
  input  halt,
  output [31:0] Insout,
  output [31:0] PCout
);

  wire not_1_out;
  wire [31:0] multiplexer_1_out, multiplexer_2_out;

  not not_1 (not_1_out, halt);
  Register #(.width(32)) register_1 (.D(multiplexer_1_out), .en(not_1_out), .Q(Insout), .clk(clk));  // open: clr
  Multiplexer #(.width(32), .enable("false")) multiplexer_1 (
    .in0(Insin), .in1({32{1'b0}}), .out(multiplexer_1_out), .sel(rst));
  Multiplexer #(.width(32), .enable("false")) multiplexer_2 (
    .in0(PCin), .in1({32{1'b0}}), .out(multiplexer_2_out), .sel(rst));
  Register #(.width(32)) register_2 (.D(multiplexer_2_out), .en(not_1_out), .Q(PCout), .clk(clk));  // open: clr
endmodule

module ID_EX (
  input  [31:0] RAin,
  input  [4:0] RDin,
  input  [4:0] RTin,
  input  [31:0] RBin,
  input  [31:0] OFFSETin,
  input  _16ExtImmin,
  input  [31:0] PCin,
  input  SextImmin,
  input  [3:0] ALUOPin,
  input  JALin,
  input  WEin,
  input  _5extImmin,
  input  SWin,
  input  SYSin,
  input  BEQ,
  input  LWin,
  input  [25:0] INDEXin,
  input  BNE,
  input  JR,
  input  J,
  input  clk,
  input  rst,
  input  halt,
  output [31:0] RAout,
  output [4:0] DESout,
  output [31:0] RBout,
  output [31:0] OFFsetout,
  output _16ExtImmout,
  output [31:0] PCout,
  output SextImmout,
  output [3:0] ALUOPout,
  output JALout,
  output WEout,
  output _5extImmout,
  output SWout,
  output SYSout,
  output BEQ_2,
  output LWout,
  output [25:0] INDEXout,
  output BNE_2,
  output JR_2,
  output J_2
);

  wire multiplexer_6_out, multiplexer_7_out, multiplexer_8_out, multiplexer_10_out, multiplexer_13_out,
       multiplexer_14_out, multiplexer_15_out, multiplexer_16_out, multiplexer_17_out, multiplexer_18_out,
       multiplexer_19_out, multiplexer_20_out, not_1_out;
  wire [0:0] or_1_out;
  wire [3:0] multiplexer_5_out;
  wire [4:0] multiplexer_11_out, multiplexer_12_out, register_11_q, register_12_q;
  wire [25:0] multiplexer_9_out;
  wire [31:0] multiplexer_1_out, multiplexer_2_out, multiplexer_3_out, multiplexer_4_out;

  not not_1 (not_1_out, halt);
  Multiplexer #(.width(32), .enable("false")) multiplexer_1 (
    .in0(RAin), .in1({32{1'b0}}), .out(multiplexer_1_out), .sel(rst));
  Multiplexer #(.width(32), .enable("false")) multiplexer_2 (
    .in0(RBin), .in1({32{1'b0}}), .out(multiplexer_2_out), .sel(rst));
  Multiplexer #(.width(32), .enable("false")) multiplexer_3 (
    .in0(OFFSETin), .in1({32{1'b0}}), .out(multiplexer_3_out), .sel(rst));
  Multiplexer #(.width(32), .enable("false")) multiplexer_4 (
    .in0(PCin), .in1({32{1'b0}}), .out(multiplexer_4_out), .sel(rst));
  Multiplexer #(.width(4), .enable("false")) multiplexer_5 (
    .in0(ALUOPin), .in1(4'b0000), .out(multiplexer_5_out), .sel(rst));
  Multiplexer #(.enable("false")) multiplexer_6 (.in0(WEin), .in1(1'b0), .out(multiplexer_6_out), .sel(rst));
  Multiplexer #(.enable("false")) multiplexer_7 (.in0(SWin), .in1(1'b0), .out(multiplexer_7_out), .sel(rst));
  Multiplexer #(.enable("false")) multiplexer_8 (.in0(LWin), .in1(1'b0), .out(multiplexer_8_out), .sel(rst));
  Multiplexer #(.width(26), .enable("false")) multiplexer_9 (
    .in0(INDEXin), .in1({26{1'b0}}), .out(multiplexer_9_out), .sel(rst));
  Multiplexer #(.enable("false")) multiplexer_10 (.in0(JR), .in1(1'b0), .out(multiplexer_10_out), .sel(rst));
  Register #(.width(32)) register_1 (.D(multiplexer_1_out), .en(not_1_out), .Q(RAout), .clk(clk));  // open: clr
  Register #(.width(32)) register_2 (.D(multiplexer_2_out), .en(not_1_out), .Q(RBout), .clk(clk));  // open: clr
  Register #(.width(32)) register_3 (.D(multiplexer_3_out), .en(not_1_out), .Q(OFFsetout), .clk(clk));  // open: clr
  Register #(.width(32)) register_4 (.D(multiplexer_4_out), .en(not_1_out), .Q(PCout), .clk(clk));  // open: clr
  Register #(.width(4)) register_5 (.D(multiplexer_5_out), .en(not_1_out), .Q(ALUOPout), .clk(clk));  // open: clr
  Register #(.width(1)) register_6 (.D(multiplexer_6_out), .en(not_1_out), .Q(WEout), .clk(clk));  // open: clr
  Register #(.width(1)) register_7 (.D(multiplexer_7_out), .en(not_1_out), .Q(SWout), .clk(clk));  // open: clr
  Register #(.width(1)) register_8 (.D(multiplexer_8_out), .en(not_1_out), .Q(LWout), .clk(clk));  // open: clr
  Register #(.width(26)) register_9 (.D(multiplexer_9_out), .en(not_1_out), .Q(INDEXout), .clk(clk));  // open: clr
  Register #(.width(1)) register_10 (.D(multiplexer_10_out), .en(not_1_out), .Q(JR_2), .clk(clk));  // open: clr
  Multiplexer #(.width(5), .enable("false")) multiplexer_11 (
    .in0(RDin), .in1({5{1'b0}}), .out(multiplexer_11_out), .sel(rst));
  Multiplexer #(.width(5), .enable("false")) multiplexer_12 (
    .in0(RTin), .in1({5{1'b0}}), .out(multiplexer_12_out), .sel(rst));
  Multiplexer #(.enable("false")) multiplexer_13 (.in0(_16ExtImmin), .in1(1'b0), .out(multiplexer_13_out), .sel(rst));
  Multiplexer #(.enable("false")) multiplexer_14 (.in0(SextImmin), .in1(1'b0), .out(multiplexer_14_out), .sel(rst));
  Multiplexer #(.enable("false")) multiplexer_15 (.in0(JALin), .in1(1'b0), .out(multiplexer_15_out), .sel(rst));
  Multiplexer #(.enable("false")) multiplexer_16 (.in0(_5extImmin), .in1(1'b0), .out(multiplexer_16_out), .sel(rst));
  Multiplexer #(.enable("false")) multiplexer_17 (.in0(SYSin), .in1(1'b0), .out(multiplexer_17_out), .sel(rst));
  Multiplexer #(.enable("false")) multiplexer_18 (.in0(BEQ), .in1(1'b0), .out(multiplexer_18_out), .sel(rst));
  Multiplexer #(.enable("false")) multiplexer_19 (.in0(BNE), .in1(1'b0), .out(multiplexer_19_out), .sel(rst));
  Multiplexer #(.enable("false")) multiplexer_20 (.in0(J), .in1(1'b0), .out(multiplexer_20_out), .sel(rst));
  Register #(.width(5)) register_11 (
    .D(multiplexer_11_out), .en(not_1_out), .Q(register_11_q), .clk(clk));  // open: clr
  Register #(.width(5)) register_12 (
    .D(multiplexer_12_out), .en(not_1_out), .Q(register_12_q), .clk(clk));  // open: clr
  Register #(.width(1)) register_13 (.D(multiplexer_13_out), .en(not_1_out), .Q(_16ExtImmout), .clk(clk));  // open: clr
  Register #(.width(1)) register_14 (.D(multiplexer_14_out), .en(not_1_out), .Q(SextImmout), .clk(clk));  // open: clr
  Register #(.width(1)) register_15 (.D(multiplexer_15_out), .en(not_1_out), .Q(JALout), .clk(clk));  // open: clr
  Register #(.width(1)) register_16 (.D(multiplexer_16_out), .en(not_1_out), .Q(_5extImmout), .clk(clk));  // open: clr
  Register #(.width(1)) register_17 (.D(multiplexer_17_out), .en(not_1_out), .Q(SYSout), .clk(clk));  // open: clr
  Register #(.width(1)) register_18 (.D(multiplexer_18_out), .en(not_1_out), .Q(BEQ_2), .clk(clk));  // open: clr
  Register #(.width(1)) register_19 (.D(multiplexer_19_out), .en(not_1_out), .Q(BNE_2), .clk(clk));  // open: clr
  Register #(.width(1)) register_20 (.D(multiplexer_20_out), .en(not_1_out), .Q(J_2), .clk(clk));  // open: clr
  Multiplexer #(.select(2), .width(5), .enable("false")) multiplexer_21 (
    .in0(register_11_q), .in1(register_12_q), .in2({5{1'b1}}), .in3({5{1'b0}}), .out(DESout),
    .sel({JALout, or_1_out[0]}));
  or or_1 (or_1_out[0], _16ExtImmout, SextImmout);
endmodule

module EX_MEM (
  input  [31:0] Rin,
  input  [31:0] RBin,
  input  [31:0] PCin,
  input  [4:0] DESin,
  input  SWin,
  input  LWin,
  input  JALin,
  input  WEin,
  input  SYSin,
  input  clk,
  input  rst,
  input  halt,
  output [31:0] Rout,
  output [31:0] RBout,
  output [31:0] PCout,
  output [4:0] DESout,
  output SWout,
  output LWout,
  output JALout,
  output WEout,
  output SYSout
);

  wire multiplexer_5_out, multiplexer_6_out, multiplexer_7_out, multiplexer_8_out, multiplexer_9_out,
       not_1_out;
  wire [4:0] multiplexer_4_out;
  wire [31:0] multiplexer_1_out, multiplexer_2_out, multiplexer_3_out;

  not not_1 (not_1_out, halt);
  Multiplexer #(.width(32), .enable("false")) multiplexer_1 (
    .in0(Rin), .in1({32{1'b0}}), .out(multiplexer_1_out), .sel(rst));
  Multiplexer #(.width(32), .enable("false")) multiplexer_2 (
    .in0(RBin), .in1({32{1'b0}}), .out(multiplexer_2_out), .sel(rst));
  Multiplexer #(.width(32), .enable("false")) multiplexer_3 (
    .in0(PCin), .in1({32{1'b0}}), .out(multiplexer_3_out), .sel(rst));
  Multiplexer #(.width(5), .enable("false")) multiplexer_4 (
    .in0(DESin), .in1({5{1'b0}}), .out(multiplexer_4_out), .sel(rst));
  Multiplexer #(.enable("false")) multiplexer_5 (.in0(SWin), .in1(1'b0), .out(multiplexer_5_out), .sel(rst));
  Multiplexer #(.enable("false")) multiplexer_6 (.in0(LWin), .in1(1'b0), .out(multiplexer_6_out), .sel(rst));
  Multiplexer #(.enable("false")) multiplexer_7 (.in0(JALin), .in1(1'b0), .out(multiplexer_7_out), .sel(rst));
  Multiplexer #(.enable("false")) multiplexer_8 (.in0(WEin), .in1(1'b0), .out(multiplexer_8_out), .sel(rst));
  Multiplexer #(.enable("false")) multiplexer_9 (.in0(SYSin), .in1(1'b0), .out(multiplexer_9_out), .sel(rst));
  Register #(.width(32)) register_1 (.D(multiplexer_1_out), .en(not_1_out), .Q(Rout), .clk(clk));  // open: clr
  Register #(.width(32)) register_2 (.D(multiplexer_2_out), .en(not_1_out), .Q(RBout), .clk(clk));  // open: clr
  Register #(.width(32)) register_3 (.D(multiplexer_3_out), .en(not_1_out), .Q(PCout), .clk(clk));  // open: clr
  Register #(.width(5)) register_4 (.D(multiplexer_4_out), .en(not_1_out), .Q(DESout), .clk(clk));  // open: clr
  Register #(.width(1)) register_5 (.D(multiplexer_5_out), .en(not_1_out), .Q(SWout), .clk(clk));  // open: clr
  Register #(.width(1)) register_6 (.D(multiplexer_6_out), .en(not_1_out), .Q(LWout), .clk(clk));  // open: clr
  Register #(.width(1)) register_7 (.D(multiplexer_7_out), .en(not_1_out), .Q(JALout), .clk(clk));  // open: clr
  Register #(.width(1)) register_8 (.D(multiplexer_8_out), .en(not_1_out), .Q(WEout), .clk(clk));  // open: clr
  Register #(.width(1)) register_9 (.D(multiplexer_9_out), .en(not_1_out), .Q(SYSout), .clk(clk));  // open: clr
endmodule

module MEM_WB (
  input  [31:0] Rin,
  input  [31:0] DATAin,
  input  [31:0] PCin,
  input  [4:0] DESin,
  input  LWin,
  input  JALin,
  input  WEin,
  input  SYSin,
  input  clk,
  input  rst,
  input  halt,
  output [31:0] Wout,
  output [4:0] rWin,
  output WEout,
  output SYSout
);

  wire multiplexer_5_out, multiplexer_6_out, multiplexer_7_out, multiplexer_8_out, not_1_out;
  wire [1:0] register_5_q;
  wire [4:0] multiplexer_4_out;
  wire [31:0] adder_1_out, multiplexer_1_out, multiplexer_2_out, multiplexer_3_out, register_1_q,
       register_2_q, register_3_q;

  not not_1 (not_1_out, halt);
  Adder #(.width(32)) adder_1 (.a(PCin), .b(32'h4), .out(adder_1_out));  // open: cin, cout
  Multiplexer #(.width(32), .enable("false")) multiplexer_1 (
    .in0(Rin), .in1({32{1'b0}}), .out(multiplexer_1_out), .sel(rst));
  Register #(.width(32)) register_1 (.D(multiplexer_1_out), .en(not_1_out), .Q(register_1_q), .clk(clk));  // open: clr
  Multiplexer #(.width(32), .enable("false")) multiplexer_2 (
    .in0(DATAin), .in1({32{1'b0}}), .out(multiplexer_2_out), .sel(rst));
  Register #(.width(32)) register_2 (.D(multiplexer_2_out), .en(not_1_out), .Q(register_2_q), .clk(clk));  // open: clr
  Register #(.width(32)) register_3 (.D(multiplexer_3_out), .en(not_1_out), .Q(register_3_q), .clk(clk));  // open: clr
  Multiplexer #(.width(32), .enable("false")) multiplexer_3 (
    .in0(adder_1_out), .in1({32{1'b0}}), .out(multiplexer_3_out), .sel(rst));
  Multiplexer #(.width(5), .enable("false")) multiplexer_4 (
    .in0(DESin), .in1({5{1'b0}}), .out(multiplexer_4_out), .sel(rst));
  Register #(.width(5)) register_4 (.D(multiplexer_4_out), .en(not_1_out), .Q(rWin), .clk(clk));  // open: clr
  Register #(.width(1)) register_5 (
    .D(multiplexer_5_out), .en(not_1_out), .Q(register_5_q[0]), .clk(clk));  // open: clr
  Multiplexer #(.enable("false")) multiplexer_5 (.in0(LWin), .in1(1'b0), .out(multiplexer_5_out), .sel(rst));
  Multiplexer #(.enable("false")) multiplexer_6 (.in0(JALin), .in1(1'b0), .out(multiplexer_6_out), .sel(rst));
  Register #(.width(1)) register_6 (
    .D(multiplexer_6_out), .en(not_1_out), .Q(register_5_q[1]), .clk(clk));  // open: clr
  Multiplexer #(.enable("false")) multiplexer_7 (.in0(WEin), .in1(1'b0), .out(multiplexer_7_out), .sel(rst));
  Register #(.width(1)) register_7 (.D(multiplexer_7_out), .en(not_1_out), .Q(WEout), .clk(clk));  // open: clr
  Multiplexer #(.enable("false")) multiplexer_8 (.in0(SYSin), .in1(1'b0), .out(multiplexer_8_out), .sel(rst));
  Register #(.width(1)) register_8 (.D(multiplexer_8_out), .en(not_1_out), .Q(SYSout), .clk(clk));  // open: clr
  Multiplexer #(.select(2), .width(32), .disabled(0), .enable("false")) multiplexer_9 (
    .in0(register_1_q), .in1(register_2_q), .in2(register_3_q), .in3({32{1'b0}}), .out(Wout),
    .sel(register_5_q));
endmodule

module Handler (
  input  [4:0] DES1,
  input  [4:0] RS,
  input  WE1,
  input  [4:0] DES2,
  input  [4:0] RT,
  input  WE2,
  input  [1:0] SRC,
  input  syscall,
  input  jal,
  output Result
);

  wire and_1_out, and_2_out, and_3_out, and_4_out, comparator_1_eq, comparator_2_eq, comparator_3_eq,
       comparator_4_eq, comparator_5_eq, comparator_6_eq, comparator_7_eq, comparator_8_eq, comparator_9_eq,
       comparator_10_eq, multiplexer_5_out, multiplexer_6_out, not_1_out, not_2_out, or_2_out, or_3_out,
       result_t;
  wire [4:0] Dnum1, Dnum2, Snum1, Snum2;

  Comparator #(.width(5)) comparator_1 (.a(Dnum1), .b(Snum1), .eq(comparator_1_eq));  // open: gt, lt
  Comparator #(.width(5)) comparator_2 (.a(Snum1), .b({5{1'b0}}), .eq(comparator_2_eq));  // open: gt, lt
  not not_1 (not_1_out, comparator_2_eq);
  Comparator #(.width(5)) comparator_3 (.a(Dnum2), .b(Snum1), .eq(comparator_3_eq));  // open: gt, lt
  Comparator #(.width(5)) comparator_4 (.a(Dnum1), .b(Snum2), .eq(comparator_4_eq));  // open: gt, lt
  Comparator #(.width(5)) comparator_5 (.a(Snum2), .b({5{1'b0}}), .eq(comparator_5_eq));  // open: gt, lt
  not not_2 (not_2_out, comparator_5_eq);
  Comparator #(.width(5)) comparator_6 (.a(Dnum2), .b(Snum2), .eq(comparator_6_eq));  // open: gt, lt
  Multiplexer #(.width(5), .enable("false")) multiplexer_1 (.in0({5{1'b0}}), .in1(DES1), .out(Dnum1), .sel(WE1));
  Multiplexer #(.width(5), .enable("false")) multiplexer_2 (.in0({5{1'b0}}), .in1(DES2), .out(Dnum2), .sel(WE2));
  and and_1 (and_1_out, comparator_1_eq, not_1_out);
  and and_2 (and_2_out, not_1_out, comparator_3_eq);
  and and_3 (and_3_out, comparator_4_eq, not_2_out);
  and and_4 (and_4_out, not_2_out, comparator_6_eq);
  or or_1 (result_t, and_1_out, and_2_out, and_3_out, and_4_out);
  Multiplexer #(.width(5), .enable("false")) multiplexer_3 (.in0({5{1'b0}}), .in1(RS), .out(Snum1), .sel(SRC[1]));
  Multiplexer #(.width(5), .enable("false")) multiplexer_4 (.in0({5{1'b0}}), .in1(RT), .out(Snum2), .sel(SRC[0]));
  Comparator #(.width(5)) comparator_7 (.a(Dnum1), .b(5'b00010), .eq(comparator_7_eq));  // open: gt, lt
  Comparator #(.width(5)) comparator_8 (.a(Dnum2), .b(5'b00010), .eq(comparator_8_eq));  // open: gt, lt
  Comparator #(.width(5)) comparator_9 (.a(Dnum1), .b({5{1'b1}}), .eq(comparator_9_eq));  // open: gt, lt
  Comparator #(.width(5)) comparator_10 (.a(Dnum2), .b({5{1'b1}}), .eq(comparator_10_eq));  // open: gt, lt
  or or_2 (or_2_out, comparator_7_eq, comparator_8_eq);
  or or_3 (or_3_out, comparator_9_eq, comparator_10_eq);
  Multiplexer #(.enable("false")) multiplexer_5 (.in0(1'b0), .in1(or_2_out), .out(multiplexer_5_out), .sel(syscall));
  Multiplexer #(.enable("false")) multiplexer_6 (.in0(1'b0), .in1(or_3_out), .out(multiplexer_6_out), .sel(jal));
  or or_4 (Result, multiplexer_5_out, result_t, multiplexer_6_out);

  // Notes on the sheet:
  //   结果为0，不插气泡
endmodule

module Branch (
  input  [31:0] PC,
  input  [31:0] OFFSET,
  input  [25:0] ins_index,
  input  [31:0] RA,
  input  JAL,
  input  JR,
  input  J,
  input  [31:0] RB,
  input  BNE,
  input  BEQ,
  output [31:0] NextPC,
  output choice
);

  wire and_1_out, and_2_out, comparator_1_eq, not_1_out;
  wire [1:0] or_1_out;
  wire [31:0] adder_1_out, adder_2_out, multiplexer_1_out;

  Comparator #(.width(32)) comparator_1 (.a(RA), .b(RB), .eq(comparator_1_eq));  // open: gt, lt
  not not_1 (not_1_out, comparator_1_eq);
  Adder #(.width(32)) adder_1 (.a(PC), .b(32'h4), .out(adder_1_out));  // open: cin, cout
  Multiplexer #(.width(32), .enable("false")) multiplexer_1 (
    .in0({PC[31:28], ins_index, 2'b00}), .in1(RA), .out(multiplexer_1_out), .sel(JR));
  and and_1 (and_1_out, not_1_out, BNE);
  and and_2 (and_2_out, comparator_1_eq, BEQ);
  Adder #(.width(32)) adder_2 (.a(adder_1_out), .b({OFFSET[29:0], 2'b00}), .out(adder_2_out));  // open: cin, cout
  or or_1 (or_1_out[0], and_1_out, and_2_out);
  or or_2 (or_1_out[1], JR, J, JAL);
  Multiplexer #(.select(2), .width(32), .enable("false")) multiplexer_2 (
    .in0(adder_1_out), .in1(adder_2_out), .in2(multiplexer_1_out), .in3({32{1'b0}}), .out(NextPC),
    .sel(or_1_out));
  or or_3 (choice, JAL, J, JR, BNE, BEQ);
endmodule
