// Logisim project cpu_benchmark.circ as structural Verilog: 11 circuits, main circuit cpu
module cpu (
);

  wire \_1号中断 , \_1号中断等待指示 , \_2号中断 , \_2号中断等待指示 , \_3号中断 , \_3号中断等待指示 , _5ExtImm, and_1_out, and_2_out,
       and_3_out, and_4_out, and_5_out, and_6_out, choice, clock, comparator_1_eq, comparator_2_eq,
       comparator_3_eq, comparator_4_eq, comparator_5_eq, comparator_6_eq, controler_1__16extimm,
       controler_1_beq, controler_1_bgtz, controler_1_bne, controler_1_eret, controler_1_j, controler_1_jal,
       controler_1_jr, controler_1_lw, controler_1_mfc, controler_1_mflo, controler_1_multu,
       controler_1_regwrite, controler_1_repc, controler_1_rint, controler_1_sextimm, controler_1_sh,
       controler_1_sw, controler_1_syscall, controler_1_wepc, controler_1_wint, d_ff_1_q, d_ff_2_q, d_ff_3_q,
       ERET, ex_mem_1_eret_2, ex_mem_1_jalout, ex_mem_1_lwout, ex_mem_1_mfc_2, ex_mem_1_mflo_2,
       ex_mem_1_multu_2, ex_mem_1_repc_2, ex_mem_1_rint_2, ex_mem_1_swout, ex_mem_1_sysout, ex_mem_1_wepc_2,
       ex_mem_1_wint_2, Go, halt, id_ex_1__5extimmout, id_ex_1__16extimmout, id_ex_1_beq_2, id_ex_1_bgtz_2,
       id_ex_1_bne_2, id_ex_1_eret_2, id_ex_1_j_2, id_ex_1_jalout, id_ex_1_jr_2, id_ex_1_lwout,
       id_ex_1_mfc_2, id_ex_1_mflo_2, id_ex_1_multu_2, id_ex_1_repc_2, id_ex_1_rint_2, id_ex_1_sextimmout,
       id_ex_1_sh_2, id_ex_1_swout, id_ex_1_sysout, id_ex_1_wepc_2, id_ex_1_wint_2, IR1, IR1_2_q, IR1_3_q,
       IR1_q, IR2, IR3, mem_wb_1_mflo_2, mem_wb_1_multu_2, mem_wb_1_sysout, MFC, multiplexer_7_out,
       multiplexer_8_out, multiplexer_9_out, not_1_out, not_2_out, not_3_out, not_4_out, not_5_out, or_2_out,
       or_3_out, or_4_out, or_8_out, or_9_out, or_10_out, or_11_out, or_12_out, or_13_out, or_15_out,
       or_16_out, or_17_out, or_18_out, pause, registerfile_1_p3, rEPC, rINT_t, RST, stall, stop, W1, W2, W3,
       WE1, WE2, wEPC, wINT, zd;
  wire [0:0] comparator_7_gt;
  wire [1:0] and_8_out, and_9_out, controler_1_src, id_ex_1_src_2, INT, INTN, multiplexer_11_out, op, RINT,
       select, \中断号 ;
  wire [1:1] and_7_out;
  wire [3:0] controler_1_aluop, id_ex_1_aluopout;
  wire [4:0] controler_1_ra, controler_1_rb, controler_1_rd, CP0, DES1, DES2, ex_mem_1_rd_2,
       id_ex_1_raaddr_2, id_ex_1_rbaddr_2, id_ex_1_rd_2, mem_wb_1_rd_2, registerfile_1_p4;
  wire [11:0] EX_PC, ID_PC, WB_PC;
  wire [15:0] \load_use次数 , \总周期数 , \无条件分支指令数 , \有条件分支成功跳转 ;
  wire [25:0] id_ex_1_indexout;
  wire [31:0] adder_1_out, bit_extender_1_out, bit_extender_2_out, branch_1_nextpc, EPC, ex_mem_1_r2out,
       ex_mem_1_ra_2, ex_mem_1_rbout, id_ex_1_offsetout, id_ex_1_raout, id_ex_1_rbout, ID_PC_t,
       if_id_1_insout, IF_PC, INT32, LO_q, mem_wb_1_r2out, mem_wb_1_wout, mips_ram_1_dataout,
       multiplexer_1_out, multiplexer_2_out, multiplexer_3_out, multiplexer_4_out, multiplexer_5_out,
       multiplexer_6_out, multiplexer_10_out, PC1, PC2, PC3, R1, R2, RA, RB, registerfile_1_p7,
       registerfile_1_p8, rom_1_data, SyscallOut, WB_R, WB_RA, wMEM, wWB;

  Button \u_总复位  (.out(RST));
  Button _1 (.out(IR1));
  Button _2 (.out(IR2));
  Button _3 (.out(IR3));
  Button \u_继续运行  (.out(Go));
  LED led_1 (.in(W1));
  LED led_2 (.in(W2));
  LED led_3 (.in(W3));
  // Probe on IF_PC[11:0]
  Comparator #(.width(32), .mode("unsigned")) comparator_1 (
    .a(PC1), .b({32{1'b0}}), .eq(comparator_1_eq));  // open: gt, lt
  Comparator #(.width(32), .mode("unsigned")) comparator_2 (
    .a(PC2), .b({32{1'b0}}), .eq(comparator_2_eq));  // open: gt, lt
  Comparator #(.width(32), .mode("unsigned")) comparator_3 (
    .a(PC3), .b({32{1'b0}}), .eq(comparator_3_eq));  // open: gt, lt
  Hex_Digit_Display hex_digit_display_1 (.value(SyscallOut[31:28]));  // open: dp
  not not_1 (not_1_out, comparator_1_eq);
  not not_2 (not_2_out, comparator_2_eq);
  not not_3 (not_3_out, comparator_3_eq);
  Hex_Digit_Display hex_digit_display_2 (.value(SyscallOut[27:24]));  // open: dp
  Hex_Digit_Display hex_digit_display_3 (.value(SyscallOut[23:20]));  // open: dp
  // Probe on ID_PC
  Clock clock_1 (.out(clock));
  Button _1_2 (.out(\_1号中断 ));
  Button _2_2 (.out(\_2号中断 ));
  Button _3_2 (.out(\_3号中断 ));
  Multiplexer #(.select(2), .width(32), .enable("false")) multiplexer_1 (
    .in0({32{1'b0}}), .in1(PC1), .in2(PC2), .in3(PC3), .out(multiplexer_1_out), .sel(select));
  Hex_Digit_Display hex_digit_display_4 (.value(SyscallOut[15:12]));  // open: dp
  Hex_Digit_Display hex_digit_display_5 (.value(SyscallOut[19:16]));  // open: dp
  LED _1_3 (.in(\_1号中断等待指示 ));
  LED _2_3 (.in(\_2号中断等待指示 ));
  LED _3_3 (.in(\_3号中断等待指示 ));
  Priority_Encoder #(.select(2)) priority_encoder_1 (
    .in1(not_1_out), .in2(not_2_out), .in3(not_3_out), .out(select));  // open: in0, gs, en_out, en_in
  Multiplexer #(.width(32), .enable("false")) multiplexer_2 (
    .in0(adder_1_out), .in1(branch_1_nextpc), .out(multiplexer_2_out), .sel(choice));
  or or_1 (zd, \中断号 [0], \中断号 [1]);
  Hex_Digit_Display hex_digit_display_6 (.value(SyscallOut[7:4]));  // open: dp
  Hex_Digit_Display hex_digit_display_7 (.value(SyscallOut[11:8]));  // open: dp
  // Probe on EX_PC
  Multiplexer #(.width(32), .enable("false")) multiplexer_3 (
    .in0({32{1'b0}}), .in1(multiplexer_1_out), .out(multiplexer_3_out), .sel(zd));
  or or_2 (or_2_out, zd, wEPC);
  Hex_Digit_Display hex_digit_display_8 (.value(SyscallOut[3:0]));  // open: dp
  // Probe on EX_PC
  // Probe on \_1号中断 
  // Probe on \_2号中断 
  // Probe on \_3号中断 
  Register #(.width(32)) register_1 (.D(multiplexer_4_out), .en(or_2_out), .Q(EPC), .clk(clock));  // open: clr
  Multiplexer #(.width(32), .enable("false")) multiplexer_4 (
    .in0(multiplexer_3_out), .in1(WB_RA), .out(multiplexer_4_out), .sel(wEPC));
  // Probe on \总周期数 
  // Probe on \无条件分支指令数 
  // Probe on \有条件分支成功跳转 
  // Probe on \load_use次数 
  // Probe on \load_use次数 
  // Probe on WB_PC
  Multiplexer #(.width(32), .enable("false")) multiplexer_5 (
    .in0(multiplexer_2_out), .in1(EPC), .out(multiplexer_5_out), .sel(ERET));
  Multiplexer #(.select(2), .width(32), .enable("false")) multiplexer_6 (
    .in0(multiplexer_5_out), .in1(32'h30cc), .in2(32'h31bc), .in3(32'h32ac), .out(multiplexer_6_out),
    .sel(\中断号 ));
  not not_4 (not_4_out, or_3_out);
  or or_3 (or_3_out, stall, halt, pause);
  Comparator #(.width(2), .mode("unsigned")) comparator_4 (.a(2'b10), .b(op), .eq(comparator_4_eq));  // open: gt, lt
  Comparator #(.width(2), .mode("unsigned")) comparator_5 (.a(2'b11), .b(op), .eq(comparator_5_eq));  // open: gt, lt
  Adder #(.width(32)) adder_1 (.a(32'h4), .b(IF_PC), .out(adder_1_out));  // open: cin, cout
  Register #(.width(32)) PC (.D(multiplexer_6_out), .en(not_4_out), .Q(IF_PC), .clk(clock), .clr(RST));
  Comparator #(.width(2), .mode("unsigned")) comparator_6 (.a(2'b01), .b(op), .eq(comparator_6_eq));  // open: gt, lt
  and and_1 (and_1_out, comparator_6_eq, ERET);
  Multiplexer #(.enable("false")) multiplexer_7 (.in0(1'b0), .in1(1'b1), .out(multiplexer_7_out), .sel(and_1_out));
  and and_2 (and_2_out, comparator_4_eq, ERET);
  Multiplexer #(.enable("false")) multiplexer_8 (.in0(1'b0), .in1(1'b1), .out(multiplexer_8_out), .sel(and_2_out));
  and and_3 (and_3_out, comparator_5_eq, ERET);
  Multiplexer #(.enable("false")) multiplexer_9 (.in0(1'b0), .in1(1'b1), .out(multiplexer_9_out), .sel(and_3_out));
  ROM #(.addrWidth(10), .dataWidth(32)) rom_1 (.addr(IF_PC[11:2]), .data(rom_1_data));  // open: sel
  or or_4 (or_4_out, choice, ERET, zd);
  or or_5 (\_1号中断等待指示 , IR1_q, d_ff_1_q);
  or or_6 (\_2号中断等待指示 , IR1_2_q, d_ff_2_q);
  or or_7 (\_3号中断等待指示 , IR1_3_q, d_ff_3_q);
  IF_ID if_id_1 (
    .Insin(rom_1_data), .PCin(IF_PC), .clk(clock), .Insout(if_id_1_insout), .PCout(ID_PC_t), .rst(or_4_out),
    .halt(or_8_out));
  // Probe on if_id_1_insout
  or or_8 (or_8_out, stall, pause);
  D_Flip_Flop d_ff_1 (.clk(\_1号中断 ), .D(1'b1), .Q(d_ff_1_q), .reset(IR1_q));  // open: Qn, preset, en
  D_Flip_Flop d_ff_2 (.clk(\_2号中断 ), .D(1'b1), .Q(d_ff_2_q), .reset(IR1_2_q));  // open: Qn, preset, en
  D_Flip_Flop d_ff_3 (.clk(\_3号中断 ), .D(1'b1), .Q(d_ff_3_q), .reset(IR1_3_q));  // open: Qn, preset, en
  Handler handler_1 (
    .DES1(DES1), .rA(controler_1_ra), .WE1(WE1), .rB(controler_1_rb), .SRC(controler_1_src), .Result(stall),
    .LW(id_ex_1_lwout), .wEPC(controler_1_wepc), .wINT(controler_1_wint));
  or or_9 (or_9_out, d_ff_1_q, IR1_q);
  or or_10 (or_10_out, d_ff_2_q, IR1_2_q);
  or or_11 (or_11_out, d_ff_3_q, IR1_3_q);
  assign bit_extender_1_out = {{16{if_id_1_insout[15]}}, if_id_1_insout[15:0]};  // Bit_Extender bit_extender_1
  assign bit_extender_2_out = {{27{1'b0}}, if_id_1_insout[10:6]};  // Bit_Extender bit_extender_2
  controler controler_1 (
    .AluOp(controler_1_aluop), .LW(controler_1_lw), ._16ExtImm(controler_1__16extimm), .JAL(controler_1_jal),
    .syscall(controler_1_syscall), .SW(controler_1_sw), .SExtImm(controler_1_sextimm), ._5ExtImm(_5ExtImm),
    .SH(controler_1_sh), .RegWrite(controler_1_regwrite), .SRC(controler_1_src), .BNE(controler_1_bne),
    .BEQ(controler_1_beq), .J(controler_1_j), .JR(controler_1_jr), .MULTU(controler_1_multu),
    .MFLO(controler_1_mflo), .BGTZ(controler_1_bgtz), .rA(controler_1_ra), .rB(controler_1_rb),
    .IM(if_id_1_insout), .ERET(controler_1_eret), .rEPC(controler_1_repc), .rINT(controler_1_rint),
    .wEPC(controler_1_wepc), .wINT(controler_1_wint), .MFC(controler_1_mfc), .RD(controler_1_rd));
  and and_4 (and_4_out, or_9_out, ~multiplexer_7_out);  // AND_Gate
  and and_5 (and_5_out, or_10_out, ~multiplexer_8_out);  // AND_Gate
  and and_6 (and_6_out, or_11_out, ~multiplexer_9_out);  // AND_Gate
  D_Flip_Flop u_IR1 (.clk(clock), .D(and_4_out), .Q(IR1_q));  // open: Qn, preset, en, reset
  D_Flip_Flop IR1_2 (.clk(clock), .D(and_5_out), .Q(IR1_2_q));  // open: Qn, preset, en, reset
  D_Flip_Flop IR1_3 (.clk(clock), .D(and_6_out), .Q(IR1_3_q));  // open: Qn, preset, en, reset
  Multiplexer #(.width(32), .enable("false")) multiplexer_10 (
    .in0(bit_extender_1_out), .in1(bit_extender_2_out), .out(multiplexer_10_out), .sel(_5ExtImm));
  Priority_Encoder #(.select(2)) priority_encoder_2 (
    .in0(1'b1), .in1(IR1_q), .in2(IR1_2_q), .in3(IR1_3_q), .out(op));  // open: gs, en_out, en_in
  and and_7 (and_7_out[1], CP0[0], not_5_out);
  not not_5 (not_5_out, MFC);
  // RegisterFile registerfile_1: pin names not known; wires that end beside it: wWB, clock, registerfile_1_p3, registerfile_1_p4, controler_1_ra, controler_1_rb, registerfile_1_p7, registerfile_1_p8
  ID_EX id_ex_1 (
    .LWin(controler_1_lw), .LWout(id_ex_1_lwout), .RAin(registerfile_1_p7), .RAout(id_ex_1_raout),
    .JALin(controler_1_jal), .JALout(id_ex_1_jalout), .RBin(registerfile_1_p8), .RBout(id_ex_1_rbout),
    .RDin(if_id_1_insout[15:11]), ._16ExtImmin(controler_1__16extimm), .RTin(if_id_1_insout[20:16]),
    .SextImmin(controler_1_sextimm), .WEin(controler_1_regwrite), .WEout(WE1), ._5extImmin(_5ExtImm),
    ._5extImmout(id_ex_1__5extimmout), .OFFSETin(multiplexer_10_out), .OFFsetout(id_ex_1_offsetout),
    .SWin(controler_1_sw), .SWout(id_ex_1_swout), .ALUOPin(controler_1_aluop), .ALUOPout(id_ex_1_aluopout),
    .PCin(ID_PC_t), .PCout(PC1), .SYSin(controler_1_syscall), .SYSout(id_ex_1_sysout), .halt(or_12_out),
    .clk(clock), .rst(or_13_out), .DESout(DES1), .SextImmout(id_ex_1_sextimmout),
    ._16ExtImmout(id_ex_1__16extimmout), .INDEXin(if_id_1_insout[25:0]), .INDEXout(id_ex_1_indexout),
    .BEQ(controler_1_beq), .BEQ_2(id_ex_1_beq_2), .BNE(controler_1_bne), .BNE_2(id_ex_1_bne_2),
    .JR(controler_1_jr), .JR_2(id_ex_1_jr_2), .J(controler_1_j), .J_2(id_ex_1_j_2),
    .MULTU(controler_1_multu), .MULTU_2(id_ex_1_multu_2), .MFLO(controler_1_mflo), .MFLO_2(id_ex_1_mflo_2),
    .BGTZ(controler_1_bgtz), .BGTZ_2(id_ex_1_bgtz_2), .SH(controler_1_sh), .SH_2(id_ex_1_sh_2),
    .rAaddr(controler_1_ra), .rAaddr_2(id_ex_1_raaddr_2), .rBaddr(controler_1_rb),
    .rBaddr_2(id_ex_1_rbaddr_2), .SRC(controler_1_src), .SRC_2(id_ex_1_src_2), .rEPC(controler_1_repc),
    .rEPC_2(id_ex_1_repc_2), .wEPC(controler_1_wepc), .wEPC_2(id_ex_1_wepc_2), .rINT(controler_1_rint),
    .rINT_2(id_ex_1_rint_2), .wINT(controler_1_wint), .wINT_2(id_ex_1_wint_2), .MFC(controler_1_mfc),
    .MFC_2(id_ex_1_mfc_2), .ERET(controler_1_eret), .ERET_2(id_ex_1_eret_2), .RD(controler_1_rd),
    .RD_2(id_ex_1_rd_2));
  or or_12 (or_12_out, halt, pause);
  or or_13 (or_13_out, zd, ERET, stop);
  or or_14 (stop, choice, stall);
  assign INT32 = {{30{1'b0}}, INT};  // Bit_Extender bit_extender_3
  // Probe on and_8_out
  assign and_8_out = op & {2{and_7_out[1]}};  // AND_Gate and_8, 2 bits wide
  // Probe on multiplexer_11_out
  Multiplexer #(.select(2), .width(2), .disabled(0), .enable("false")) multiplexer_11 (
    .in0(2'b00), .in1(and_8_out), .in2(RINT), .in3(and_8_out), .out(multiplexer_11_out),
    .sel({ERET, comparator_7_gt[0]}));
  Comparator #(.width(2), .mode("unsigned")) comparator_7 (
    .a(and_8_out), .b(INTN), .gt(comparator_7_gt[0]));  // open: eq, lt
  or or_15 (or_15_out, id_ex_1__16extimmout, id_ex_1_sextimmout, id_ex_1__5extimmout);
  Redirection redirection_1 (
    .RA(id_ex_1_raout), .wMEM(wMEM), .RB(id_ex_1_rbout), .wWB(wWB), ._5ext(id_ex_1__5extimmout),
    .Offset(id_ex_1_offsetout), .ext(or_15_out), .ALUop(id_ex_1_aluopout), .rA_2(id_ex_1_raaddr_2),
    .DES1(DES2), .WE1(WE2), .rB_2(id_ex_1_rbaddr_2), .DES2(registerfile_1_p4), .WE2(registerfile_1_p3),
    .Result1(R1), .RAout(RA), .Result2(R2), .RBout(RB), .SRC(id_ex_1_src_2), .mflo(ex_mem_1_mflo_2),
    .WB_R(WB_R), .wEPC(id_ex_1_wepc_2), .wINT(id_ex_1_wint_2));
  or or_16 (or_16_out, comparator_7_gt[0], ERET);
  Register #(.width(2)) register_2 (.D(multiplexer_11_out), .en(or_16_out), .Q(INTN), .clk(clock));  // open: clr
  Branch branch_1 (
    .PC(PC1), .OFFSET(id_ex_1_offsetout), .ins_index(id_ex_1_indexout), .RA(RA), .RB(RB),
    .BNE(id_ex_1_bne_2), .BEQ(id_ex_1_beq_2), .NextPC(branch_1_nextpc), .JR(id_ex_1_jr_2), .J(id_ex_1_j_2),
    .JAL(id_ex_1_jalout), .choice(choice), .BGTZ(id_ex_1_bgtz_2), .un(\无条件分支指令数 ), .success(\有条件分支成功跳转 ),
    .clk(clock));
  Register #(.width(2)) register_3 (.D(INTN), .en(or_16_out), .Q(INT), .clk(clock));  // open: clr
  // Probe on INTN
  Register #(.width(2)) register_4 (.D(WB_RA[1:0]), .en(wINT), .Q(RINT), .clk(clock));  // open: clr
  // Probe on \中断号 
  Multiplexer #(.width(2), .enable("false")) multiplexer_12 (
    .in0(2'b00), .in1(multiplexer_11_out), .out(\中断号 ), .sel(comparator_7_gt[0]));
  // Probe on multiplexer_11_out
  or or_17 (or_17_out, zd, ERET);
  EX_MEM ex_mem_1 (
    .LWin(id_ex_1_lwout), .LWout(ex_mem_1_lwout), .Rin(R1), .Rout(wMEM), .JALin(id_ex_1_jalout),
    .JALout(ex_mem_1_jalout), .RBin(RB), .RBout(ex_mem_1_rbout), .SWin(id_ex_1_swout),
    .SWout(ex_mem_1_swout), .PCin(PC1), .PCout(PC2), .clk(clock), .WEin(WE1), .WEout(WE2), .rst(or_17_out),
    .halt(or_12_out), .SYSin(id_ex_1_sysout), .SYSout(ex_mem_1_sysout), .DESin(DES1), .DESout(DES2),
    .R2in(R2), .R2out(ex_mem_1_r2out), .MULTU(id_ex_1_multu_2), .MULTU_2(ex_mem_1_multu_2),
    .MFLO(id_ex_1_mflo_2), .MFLO_2(ex_mem_1_mflo_2), .SH(id_ex_1_sh_2), .SH_2(and_9_out[1]), .RA(RA),
    .RA_2(ex_mem_1_ra_2), .wINT(id_ex_1_wint_2), .wINT_2(ex_mem_1_wint_2), .ERET(id_ex_1_eret_2),
    .ERET_2(ex_mem_1_eret_2), .rEPC(id_ex_1_repc_2), .rEPC_2(ex_mem_1_repc_2), .rINT(id_ex_1_rint_2),
    .rINT_2(ex_mem_1_rint_2), .wEPC(id_ex_1_wepc_2), .wEPC_2(ex_mem_1_wepc_2), .MFC(id_ex_1_mfc_2),
    .MFC_2(ex_mem_1_mfc_2), .RD(id_ex_1_rd_2), .RD_2(ex_mem_1_rd_2));
  Statistics statistics_1 (
    .stall(stall), .RAsys(WB_RA), .syscall(mem_wb_1_sysout), .clk(clock), .RB(RB), .disp(id_ex_1_sysout),
    .Go(Go), .RA(RA), .pause(pause), .\总周期数 (\总周期数 ), .halt(halt), .\插入气泡数 (\load_use次数 ),
    .SyscallOut(SyscallOut));
  MIPS_RAM mips_ram_1 (
    .\字节地址 (wMEM[11:0]), .Din(ex_mem_1_rbout), .DataOut(mips_ram_1_dataout), .CLK(clock), .WE(or_18_out),
    .Mode(and_9_out), .RST(RST));
  or or_18 (or_18_out, ex_mem_1_swout, and_9_out[1]);
  MEM_WB mem_wb_1 (
    .Rin(wMEM), .DATAin(mips_ram_1_dataout), .clk(clock), .PCin(PC2), .Wout(mem_wb_1_wout),
    .LWin(ex_mem_1_lwout), .JALin(ex_mem_1_jalout), .WEin(WE2), .WEout(registerfile_1_p3), .rst(zd),
    .halt(or_12_out), .SYSout(mem_wb_1_sysout), .SYSin(ex_mem_1_sysout), .DESin(DES2),
    .rWin(registerfile_1_p4), .R2in(ex_mem_1_r2out), .R2out(mem_wb_1_r2out), .Rout(WB_R),
    .MULTU(ex_mem_1_multu_2), .MULTU_2(mem_wb_1_multu_2), .MFLO(ex_mem_1_mflo_2), .MFLO_2(mem_wb_1_mflo_2),
    .RA(ex_mem_1_ra_2), .RA_2(WB_RA), .PC(PC3), .ERET(ex_mem_1_eret_2), .ERET_2(ERET),
    .wEPC(ex_mem_1_wepc_2), .wEPC_2(wEPC), .wINT(ex_mem_1_wint_2), .wINT_2(wINT), .rEPC(ex_mem_1_repc_2),
    .rEPC_2(rEPC), .rINT(ex_mem_1_rint_2), .rINT_2(rINT_t), .MFC(ex_mem_1_mfc_2), .MFC_2(MFC),
    .RD(ex_mem_1_rd_2), .RD_2(mem_wb_1_rd_2), .EPC(EPC), .INT32(INT32));
  and and_9 (and_9_out[0], ~and_9_out[1], ~ex_mem_1_swout, ~ex_mem_1_lwout);  // AND_Gate
  Register #(.width(32)) LO (.D(WB_R), .en(mem_wb_1_multu_2), .Q(LO_q), .clk(clock));  // open: clr
  Register #(.width(32)) HI (.D(mem_wb_1_r2out), .en(mem_wb_1_multu_2), .clk(clock));  // open: Q, clr
  Register #(.width(5)) register_5 (.D(mem_wb_1_rd_2), .en(MFC), .Q(CP0), .clk(clock));  // open: clr
  Multiplexer #(.width(32), .enable("false")) multiplexer_13 (
    .in0(mem_wb_1_wout), .in1(LO_q), .out(wWB), .sel(mem_wb_1_mflo_2));

  // Other names for the same wires on the sheet: 插入气泡数[15:0] = \load_use次数 

  // Notes on the sheet:
  //   中断源
  //   中断请求指示
  //   数码管输出应该用寄存器锁存，否则显示数据只能一闪而过
  //   可以通过项目增加Logisim库的方式将前几次实验完成的电路作为子电路引入到本电路中使用
  //   数码管输出
  //   中断信号源及指示电路规范（优先级3>2>1>CPU(0）)
  //   总复位信号应将除ROM以外所有存储组件全部清零
  //   指令存储器
  //   contents of rom_1 (hex, n*v repeats v):
  //   40090800 20110200 20020022 112020 c 2231ffff 1620fffc 20020032 c 20080002 20111111 112020 20020022 c
  //   200b0020 2280019 8812 112020 20020022 c 216bffff 1560fff9 20090000 200b0020 20110001 20120001
  //   a5310000 112020 20020022 c 2328820 21290002 216bffff 1560fff8 200b0010 20090000 8d310000 112020
  //   20020022 c 21290004 216bffff 1560fff9 2011000f 112020 20020022 c 2231ffff 1e20fffb 2002000a c
  //   40110000 ac1d0230 201d0080 27bdfffc afa40000 27bdfffc afa20000 27bdfffc afb30000 27bdfffc afb40000
  //   27bdfffc afb50000 27bdfffc afb60000 27bdfffc afb00000 40101000 27bdfffc afb00000 40101800 27bdfffc
  //   afb00000 40110800 20160001 20140006 20150001 168020 108100 2149825 132020 20020022 c 1600fffa
  //   295a022 1680fff7 40110000 8fb00000 40901800 27bd0004 8fb00000 40901000 27bd0004 8fb00000 27bd0004
  //   8fb60000 27bd0004 8fb50000 27bd0004 8fb40000 27bd0004 8fb30000 27bd0004 8fa20000 27bd0004 8fa40000
  //   27bd0004 8c1d0230 42000018 40110800 40110000 ac1d0244 201d0100 27bdfffc afa40000 27bdfffc afa20000
  //   27bdfffc afb30000 27bdfffc afb40000 27bdfffc afb50000 27bdfffc afb60000 27bdfffc afb00000 40101000
  //   27bdfffc afb00000 40101800 27bdfffc afb00000 40110800 20160002 20140006 20150001 168020 108100
  //   2149825 132020 20020022 c 1600fffa 295a022 1680fff7 40110000 8fb00000 40901800 27bd0004 8fb00000
  //   40901000 27bd0004 8fb00000 27bd0004 8fb60000 27bd0004 8fb50000 27bd0004 8fb40000 27bd0004 8fb30000
  //   27bd0004 8fa20000 27bd0004 8fa40000 27bd0004 8c1d0244 42000018 40110800 40110000 ac1d0258 201d0200
  //   27bdfffc afa40000 27bdfffc afa20000 27bdfffc afb30000 27bdfffc afb40000 27bdfffc afb50000 27bdfffc
  //   afb60000 27bdfffc afb00000 40101000 27bdfffc afb00000 40101800 27bdfffc afb00000 40110800 20160003
  //   20140006 20150001 168020 108100 2149825 132020 20020022 c 1600fffa 295a022 1680fff7 40110000
  //   8fb00000 40901800 27bd0004 8fb00000 40901000 27bd0004 8fb00000 27bd0004 8fb60000 27bd0004 8fb50000
  //   27bd0004 8fb40000 27bd0004 8fb30000 27bd0004 8fa20000 27bd0004 8fa40000 27bd0004 8fa40000 8c1d0258
  //   42000018 40110800
  //   Reset 
  //   Reset 
  //   Reset 
  //   寄存器文件
endmodule

module controler (
  input  [31:0] IM,
  output syscall,
  output _16ExtImm,
  output SExtImm,
  output _5ExtImm,
  output BNE,
  output J,
  output rEPC,
  output rINT,
  output JR,
  output [3:0] AluOp,
  output wEPC,
  output wINT,
  output LW,
  output SW,
  output SH,
  output BEQ,
  output [4:0] rA,
  output RegWrite,
  output MFC,
  output ERET,
  output MULTU,
  output JAL,
  output MFLO,
  output BGTZ,
  output [4:0] rB,
  output [4:0] RD,
  output [1:0] SRC
);

  wire ADD, ADDI, ADDIU, ADDU, AND, ANDI, comparator_15_eq, comparator_16_eq, comparator_17_eq,
       comparator_18_eq, comparator_19_eq, comparator_20_eq, comparator_21_eq, comparator_22_eq,
       comparator_23_eq, comparator_24_eq, comparator_25_eq, comparator_26_eq, comparator_27_eq,
       comparator_28_eq, comparator_29_eq, comparator_30_eq, comparator_31_eq, comparator_32_eq,
       comparator_33_eq, comparator_34_eq, comparator_35_eq, comparator_36_eq, NOR, OR, or_9_out, ORI, R1,
       SLL, SLLV, sllv_srlv, SLT, SLTI, SLTU, SRA, SRL, SRLV, SUB;
  wire [1:0] multiplexer_4_out, or_10_out;
  wire [3:0] and_19_out, and_20_out, and_21_out, and_22_out, and_23_out, and_24_out, and_25_out, and_26_out,
       and_27_out, and_28_out, and_29_out;
  wire [3:3] or_2_out, or_3_out, or_4_out, or_5_out, or_6_out, or_7_out;
  wire [4:0] multiplexer_1_out;

  Comparator #(.width(6)) comparator_1 (.a(IM[31:26]), .b({6{1'b0}}), .eq(R1));  // open: gt, lt
  Comparator #(.width(6)) comparator_2 (.a(IM[31:26]), .b(6'b000010), .eq(J));  // open: gt, lt
  Comparator #(.width(6)) comparator_3 (.a(IM[31:26]), .b(6'b000011), .eq(JAL));  // open: gt, lt
  Comparator #(.width(6)) comparator_4 (.a(IM[31:26]), .b(6'b000100), .eq(BEQ));  // open: gt, lt
  Comparator #(.width(6)) comparator_5 (.a(IM[31:26]), .b(6'b000101), .eq(BNE));  // open: gt, lt
  Comparator #(.width(6)) comparator_6 (.a(IM[31:26]), .b(6'b000111), .eq(BGTZ));  // open: gt, lt
  Comparator #(.width(6)) comparator_7 (.a(IM[31:26]), .b(6'b001000), .eq(ADDI));  // open: gt, lt
  Comparator #(.width(6)) comparator_8 (.a(IM[31:26]), .b(6'b001001), .eq(ADDIU));  // open: gt, lt
  Comparator #(.width(6)) comparator_9 (.a(IM[31:26]), .b(6'b001010), .eq(SLTI));  // open: gt, lt
  Comparator #(.width(6)) comparator_10 (.a(IM[31:26]), .b(6'b001100), .eq(ANDI));  // open: gt, lt
  Comparator #(.width(6)) comparator_11 (.a(IM[31:26]), .b(6'b001101), .eq(ORI));  // open: gt, lt
  Comparator #(.width(6)) comparator_12 (.a(IM[31:26]), .b(6'b100011), .eq(LW));  // open: gt, lt
  Comparator #(.width(6)) comparator_13 (.a(IM[31:26]), .b(6'b101001), .eq(SH));  // open: gt, lt
  Comparator #(.width(6)) comparator_14 (.a(IM[31:26]), .b(6'b101011), .eq(SW));  // open: gt, lt
  Comparator #(.width(6)) comparator_15 (.a(IM[5:0]), .b({6{1'b0}}), .eq(comparator_15_eq));  // open: gt, lt
  Comparator #(.width(6)) comparator_16 (.a(IM[5:0]), .b(6'b000010), .eq(comparator_16_eq));  // open: gt, lt
  Comparator #(.width(6)) comparator_17 (.a(IM[5:0]), .b(6'b000011), .eq(comparator_17_eq));  // open: gt, lt
  Comparator #(.width(6)) comparator_18 (.a(IM[5:0]), .b(6'b000100), .eq(comparator_18_eq));  // open: gt, lt
  Comparator #(.width(6)) comparator_19 (.a(IM[5:0]), .b(6'b000110), .eq(comparator_19_eq));  // open: gt, lt
  Comparator #(.width(6)) comparator_20 (.a(IM[5:0]), .b(6'b001000), .eq(comparator_20_eq));  // open: gt, lt
  Comparator #(.width(6)) comparator_21 (.a(IM[5:0]), .b(6'b001100), .eq(comparator_21_eq));  // open: gt, lt
  Comparator #(.width(6)) comparator_22 (.a(IM[5:0]), .b(6'b010010), .eq(comparator_22_eq));  // open: gt, lt
  Comparator #(.width(6)) comparator_23 (.a(IM[5:0]), .b(6'b011001), .eq(comparator_23_eq));  // open: gt, lt
  Comparator #(.width(6)) comparator_24 (.a(IM[5:0]), .b(6'b100000), .eq(comparator_24_eq));  // open: gt, lt
  Comparator #(.width(6)) comparator_25 (.a(IM[5:0]), .b(6'b100001), .eq(comparator_25_eq));  // open: gt, lt
  Comparator #(.width(6)) comparator_26 (.a(IM[5:0]), .b(6'b100010), .eq(comparator_26_eq));  // open: gt, lt
  Comparator #(.width(6)) comparator_27 (.a(IM[5:0]), .b(6'b100100), .eq(comparator_27_eq));  // open: gt, lt
  Comparator #(.width(6)) comparator_28 (.a(IM[5:0]), .b(6'b100101), .eq(comparator_28_eq));  // open: gt, lt
  Comparator #(.width(6)) comparator_29 (.a(IM[5:0]), .b(6'b100111), .eq(comparator_29_eq));  // open: gt, lt
  Comparator #(.width(6)) comparator_30 (.a(IM[5:0]), .b(6'b101010), .eq(comparator_30_eq));  // open: gt, lt
  Comparator #(.width(6)) comparator_31 (.a(IM[5:0]), .b(6'b101011), .eq(comparator_31_eq));  // open: gt, lt
  and and_1 (SLL, R1, comparator_15_eq);
  and and_2 (SRL, R1, comparator_16_eq);
  and and_3 (SRA, R1, comparator_17_eq);
  and and_4 (SLLV, R1, comparator_18_eq);
  and and_5 (SRLV, R1, comparator_19_eq);
  and and_6 (JR, R1, comparator_20_eq);
  and and_7 (syscall, R1, comparator_21_eq);
  and and_8 (MFLO, R1, comparator_22_eq);
  and and_9 (MULTU, R1, comparator_23_eq);
  and and_10 (ADD, R1, comparator_24_eq);
  and and_11 (ADDU, R1, comparator_25_eq);
  and and_12 (SUB, R1, comparator_26_eq);
  and and_13 (AND, R1, comparator_27_eq);
  and and_14 (OR, R1, comparator_28_eq);
  and and_15 (NOR, R1, comparator_29_eq);
  and and_16 (SLT, R1, comparator_30_eq);
  and and_17 (SLTU, R1, comparator_31_eq);
  Comparator #(.width(6)) comparator_32 (.a(IM[31:26]), .b(6'b010000), .eq(comparator_32_eq));  // open: gt, lt
  Comparator #(.width(6)) comparator_33 (.a(IM[5:0]), .b(6'b011000), .eq(comparator_33_eq));  // open: gt, lt
  Comparator #(.width(32)) comparator_34 (.a(IM), .b(32'h40090800), .eq(comparator_34_eq));  // open: gt, lt
  and and_18 (ERET, comparator_32_eq, comparator_33_eq);
  Comparator #(.width(32)) comparator_35 (.a(IM), .b(32'h40110800), .eq(comparator_35_eq));  // open: gt, lt
  Comparator #(.width(32)) comparator_36 (.a(IM), .b(32'h40110000), .eq(comparator_36_eq));  // open: gt, lt
  or or_1 (MFC, comparator_35_eq, comparator_34_eq, comparator_36_eq);
  or or_2 (or_2_out[3], ADD, ADDI, ADDU, ADDIU, SW, LW, SH);
  or or_3 (or_3_out[3], AND, ANDI);
  or or_4 (or_4_out[3], OR, ORI);
  or or_5 (or_5_out[3], SLL, SLLV);
  or or_6 (or_6_out[3], SLT, SLTI);
  or or_7 (or_7_out[3], SRL, SRLV);
  assign and_19_out = 4'b0101 & {4{or_2_out[3]}};  // AND_Gate and_19, 4 bits wide
  assign and_20_out = 4'b0111 & {4{or_3_out[3]}};  // AND_Gate and_20, 4 bits wide
  assign and_21_out = 4'b1000 & {4{or_4_out[3]}};  // AND_Gate and_21, 4 bits wide
  assign and_22_out = 4'b0000 & {4{or_5_out[3]}};  // AND_Gate and_22, 4 bits wide
  assign and_23_out = 4'b1010 & {4{NOR}};  // AND_Gate and_23, 4 bits wide
  assign and_24_out = 4'b0011 & {4{MULTU}};  // AND_Gate and_24, 4 bits wide
  assign and_25_out = 4'b0001 & {4{SRA}};  // AND_Gate and_25, 4 bits wide
  assign and_26_out = 4'b1011 & {4{or_6_out[3]}};  // AND_Gate and_26, 4 bits wide
  assign and_27_out = 4'b1100 & {4{SLTU}};  // AND_Gate and_27, 4 bits wide
  assign and_28_out = 4'b0110 & {4{SUB}};  // AND_Gate and_28, 4 bits wide
  assign and_29_out = 4'b0010 & {4{or_7_out[3]}};  // AND_Gate and_29, 4 bits wide
  Comparator #(.width(32)) comparator_37 (.a(IM), .b(32'h40101000), .eq(rEPC));  // open: gt, lt
  Comparator #(.width(32)) comparator_38 (.a(IM), .b(32'h40901000), .eq(wEPC));  // open: gt, lt
  assign AluOp = and_19_out | and_20_out | and_21_out | and_22_out | and_23_out | and_24_out | and_25_out | and_26_out | and_27_out | and_28_out | and_29_out;  // OR_Gate or_8, 4 bits wide
  or or_9 (or_9_out, wINT, wEPC);
  Multiplexer #(.width(5), .enable("false")) multiplexer_1 (
    .in0(IM[25:21]), .in1(5'b00010), .out(multiplexer_1_out), .sel(syscall));
  Comparator #(.width(32)) comparator_39 (.a(IM), .b(32'h40101800), .eq(rINT));  // open: gt, lt
  Comparator #(.width(32)) comparator_40 (.a(IM), .b(32'h40901800), .eq(wINT));  // open: gt, lt
  or or_10 (or_10_out[0], SLL, SH, R1, SW, BGTZ, BEQ, BNE, SRL, SRA);
  or or_11 (or_10_out[1], SH, ANDI, ADDIU, ADDI, R1, SW, BNE, BEQ, ORI, LW, SLTI, BGTZ);
  Multiplexer #(.width(5), .enable("false")) multiplexer_2 (
    .in0(multiplexer_1_out), .in1(5'b10000), .out(rA), .sel(or_9_out));
  or or_12 (_16ExtImm, ANDI, ORI);
  or or_13 (SExtImm, ADDI, ADDIU, LW, SW, SH, BNE, BGTZ, BEQ, SLTI);
  or or_14 (_5ExtImm, SLL, SRA, SRL);
  or or_15 (sllv_srlv, SRLV, SLLV);
  Multiplexer #(.width(5), .enable("false")) multiplexer_3 (.in0(IM[20:16]), .in1(5'b00100), .out(rB), .sel(syscall));
  Multiplexer #(.width(2), .enable("false")) multiplexer_4 (
    .in0(or_10_out), .in1(2'b10), .out(multiplexer_4_out), .sel(JR));
  Multiplexer #(.width(2), .enable("false")) multiplexer_5 (
    .in0(multiplexer_4_out), .in1(2'b00), .out(SRC), .sel(MFLO));
  or or_16 (RegWrite, rINT, SRLV, ADD, ADDU, ADDI, ADDIU, AND, ANDI, SLL, SLLV, SRL, MFLO, SRA, OR, ORI, NOR, SLT, SLTU, SLTI, SUB, JAL, LW, rEPC);

  assign RD = IM[15:11];

  // Other names for the same wires on the sheet: func[5:0] = IM[5:0]; SHAMT[4:0] = IM[10:6]; RT[4:0] = IM[20:16];
  //   RS[4:0] = IM[25:21]; operate[5:0] = IM[31:26]
endmodule

module NPC (
  input  Reset,
  input  CLK,
  input  [31:0] IM,
  input  [31:0] PC,
  input  [31:0] RegRS,
  input  [31:0] RegRT,
  input  [31:0] OFFSET,
  output [31:0] NextPC,
  output [15:0] unconditional,
  output [15:0] conditional,
  output [15:0] conditionalsucces
);

  wire and_3_out, and_4_out, and_5_out, BEQ, BGTZ, BNE, comparator_1_eq, comparator_2_eq, comparator_3_eq,
       comparator_4_eq, comparator_4_gt, comparator_10_eq, halt, J, JAL, JR, not_1_out, not_2_out, or_3_out,
       or_4_out, syscall;
  wire [1:0] or_2_out;
  wire [31:0] adder_1_out, adder_2_out, multiplexer_1_out, multiplexer_2_out;

  Multiplexer #(.width(32), .enable("false")) multiplexer_1 (
    .in0(RegRT), .in1({32{1'b0}}), .out(multiplexer_1_out), .sel(BGTZ));
  // Probe on PC
  Comparator #(.width(6)) comparator_1 (.a(IM[5:0]), .b(6'b001000), .eq(comparator_1_eq));  // open: gt, lt
  Comparator #(.width(6)) comparator_2 (.a(IM[31:26]), .b({6{1'b0}}), .eq(comparator_2_eq));  // open: gt, lt
  Comparator #(.width(6)) comparator_3 (.a(IM[5:0]), .b(6'b001100), .eq(comparator_3_eq));  // open: gt, lt
  Adder #(.width(32)) adder_1 (.a(PC), .b(32'h4), .out(adder_1_out));  // open: cin, cout
  Multiplexer #(.width(32), .enable("false")) multiplexer_2 (
    .in0({PC[31:28], IM[25:0], 2'b00}), .in1(RegRS), .out(multiplexer_2_out), .sel(JR));
  Adder #(.width(32)) adder_2 (.a({OFFSET[29:0], 2'b00}), .b(adder_1_out), .out(adder_2_out));  // open: cin, cout
  Comparator #(.width(32)) comparator_4 (
    .a(RegRS), .b(multiplexer_1_out), .gt(comparator_4_gt), .eq(comparator_4_eq));  // open: lt
  Comparator #(.width(6)) comparator_5 (.a(IM[31:26]), .b(6'b000010), .eq(J));  // open: gt, lt
  Comparator #(.width(6)) comparator_6 (.a(IM[31:26]), .b(6'b000011), .eq(JAL));  // open: gt, lt
  and and_1 (JR, comparator_1_eq, comparator_2_eq);
  and and_2 (syscall, comparator_2_eq, comparator_3_eq);
  not not_1 (not_1_out, comparator_4_eq);
  and and_3 (and_3_out, BGTZ, comparator_4_gt);
  and and_4 (and_4_out, not_1_out, BNE);
  and and_5 (and_5_out, comparator_4_eq, BEQ);
  Multiplexer #(.select(2), .width(32)) multiplexer_3 (
    .in0(adder_1_out), .in1(adder_2_out), .in2(multiplexer_2_out), .out(NextPC), .sel(or_2_out),
    .en(not_2_out));  // open: in3
  or or_1 (or_2_out[1], J, JAL, JR);
  or or_2 (or_2_out[0], and_3_out, and_4_out, and_5_out);
  Comparator #(.width(6)) comparator_7 (.a(IM[31:26]), .b(6'b000101), .eq(BNE));  // open: gt, lt
  Comparator #(.width(6)) comparator_8 (.a(IM[31:26]), .b(6'b000111), .eq(BGTZ));  // open: gt, lt
  Comparator #(.width(6)) comparator_9 (.a(IM[31:26]), .b(6'b000100), .eq(BEQ));  // open: gt, lt
  Comparator #(.width(32)) comparator_10 (.a(RegRS), .b(32'ha), .eq(comparator_10_eq));  // open: gt, lt
  not not_2 (not_2_out, Reset);
  and and_6 (halt, comparator_10_eq, syscall);
  or or_3 (or_3_out, J, JAL, JR);
  or or_4 (or_4_out, BNE, BGTZ, BEQ);
  Counter #(.width(16), .max('hffff)) counter_1 (
    .count(or_3_out), .Q(unconditional), .clk(CLK), .clr(Reset));  // open: load, D, carry
  Counter #(.width(16), .max('hffff)) counter_2 (
    .count(or_4_out), .Q(conditional), .clk(CLK), .clr(Reset));  // open: load, D, carry
  Counter #(.width(16), .max('hffff)) counter_3 (
    .count(or_2_out[0]), .Q(conditionalsucces), .clk(CLK), .clr(Reset));  // open: load, D, carry

  // Other names for the same wires on the sheet: func[5:0] = IM[5:0]; instr_index[25:0] = IM[25:0];
  //   operate[5:0] = IM[31:26]; 无条件分支指令数[15:0] = unconditional; 有条件分支成功跳转[15:0] = conditionalsucces;
  //   有条件分支指令数[15:0] = conditional
endmodule

module IF_ID (
  input  [31:0] Insin,
  input  [31:0] PCin,
  input  clk,
  input  rst,
  input  halt,
  output [31:0] Insout,
  output [31:0] PCout
);

  wire not_1_out;
  wire [31:0] multiplexer_1_out, multiplexer_2_out;

  not not_1 (not_1_out, halt);
  Register #(.width(32)) register_1 (.D(multiplexer_1_out), .en(not_1_out), .Q(Insout), .clk(clk));  // open: clr
  Multiplexer #(.width(32), .enable("false")) multiplexer_1 (
    .in0(Insin), .in1({32{1'b0}}), .out(multiplexer_1_out), .sel(rst));
  Multiplexer #(.width(32), .enable("false")) multiplexer_2 (
    .in0(PCin), .in1({32{1'b0}}), .out(multiplexer_2_out), .sel(rst));
  Register #(.width(32)) register_2 (.D(multiplexer_2_out), .en(not_1_out), .Q(PCout), .clk(clk));  // open: clr
endmodule

module ID_EX (
  input  [31:0] RAin,
  input  [4:0] RDin,
  input  [4:0] RTin,
  input  [31:0] RBin,
  input  [31:0] OFFSETin,
  input  _16ExtImmin,
  input  [31:0] PCin,
  input  SextImmin,
  input  [3:0] ALUOPin,
  input  JALin,
  input  WEin,
  input  _5extImmin,
  input  SWin,
  input  SYSin,
  input  BEQ,
  input  LWin,
  input  [25:0] INDEXin,
  input  BNE,
  input  JR,
  input  J,
  input  MFLO,
  input  MULTU,
  input  BGTZ,
  input  SH,
  input  [1:0] SRC,
  input  [4:0] rAaddr,
  input  rEPC,
  input  [4:0] rBaddr,
  input  wEPC,
  input  rINT,
  input  wINT,
  input  MFC,
  input  ERET,
  input  [4:0] RD,
  input  clk,
  input  rst,
  input  halt,
  output [31:0] RAout,
  output [31:0] RBout,
  output [4:0] DESout,
  output [31:0] OFFsetout,
  output _16ExtImmout,
  output [31:0] PCout,
  output SextImmout,
  output [3:0] ALUOPout,
  output JALout,
  output WEout,
  output _5extImmout,
  output SWout,
  output SYSout,
  output BEQ_2,
  output LWout,
  output [25:0] INDEXout,
  output BNE_2,
  output JR_2,
  output J_2,
  output MFLO_2,
  output MULTU_2,
  output BGTZ_2,
  output SH_2,
  output [1:0] SRC_2,
  output [4:0] rAaddr_2,
  output rEPC_2,
  output [4:0] rBaddr_2,
  output wEPC_2,
  output rINT_2,
  output wINT_2,
  output MFC_2,
  output ERET_2,
  output [4:0] RD_2
);

  wire multiplexer_6_out, multiplexer_7_out, multiplexer_8_out, multiplexer_10_out, multiplexer_11_out,
       multiplexer_12_out, multiplexer_15_out, multiplexer_16_out, multiplexer_17_out, multiplexer_20_out,
       multiplexer_21_out, multiplexer_22_out, multiplexer_23_out, multiplexer_24_out, multiplexer_25_out,
       multiplexer_26_out, multiplexer_27_out, multiplexer_28_out, multiplexer_29_out, multiplexer_31_out,
       multiplexer_32_out, multiplexer_33_out, not_1_out, or_2_out;
  wire [0:0] or_1_out;
  wire [1:0] multiplexer_30_out;
  wire [3:0] multiplexer_5_out;
  wire [4:0] multiplexer_13_out, multiplexer_14_out, multiplexer_18_out, multiplexer_19_out,
       multiplexer_34_out, multiplexer_35_out, register_18_q, register_19_q;
  wire [25:0] multiplexer_9_out;
  wire [31:0] multiplexer_1_out, multiplexer_2_out, multiplexer_3_out, multiplexer_4_out;

  not not_1 (not_1_out, halt);
  Multiplexer #(.width(32), .enable("false")) multiplexer_1 (
    .in0(RAin), .in1({32{1'b0}}), .out(multiplexer_1_out), .sel(rst));
  Multiplexer #(.width(32), .enable("false")) multiplexer_2 (
    .in0(RBin), .in1({32{1'b0}}), .out(multiplexer_2_out), .sel(rst));
  Multiplexer #(.width(32), .enable("false")) multiplexer_3 (
    .in0(OFFSETin), .in1({32{1'b0}}), .out(multiplexer_3_out), .sel(rst));
  Multiplexer #(.width(32), .enable("false")) multiplexer_4 (
    .in0(PCin), .in1({32{1'b0}}), .out(multiplexer_4_out), .sel(rst));
  Multiplexer #(.width(4), .enable("false")) multiplexer_5 (
    .in0(ALUOPin), .in1(4'b0000), .out(multiplexer_5_out), .sel(rst));
  Multiplexer #(.enable("false")) multiplexer_6 (.in0(WEin), .in1(1'b0), .out(multiplexer_6_out), .sel(rst));
  Multiplexer #(.enable("false")) multiplexer_7 (.in0(SWin), .in1(1'b0), .out(multiplexer_7_out), .sel(rst));
  Multiplexer #(.enable("false")) multiplexer_8 (.in0(LWin), .in1(1'b0), .out(multiplexer_8_out), .sel(rst));
  Multiplexer #(.width(26), .enable("false")) multiplexer_9 (
    .in0(INDEXin), .in1({26{1'b0}}), .out(multiplexer_9_out), .sel(rst));
  Multiplexer #(.enable("false")) multiplexer_10 (.in0(JR), .in1(1'b0), .out(multiplexer_10_out), .sel(rst));
  Multiplexer #(.enable("false")) multiplexer_11 (.in0(MFLO), .in1(1'b0), .out(multiplexer_11_out), .sel(rst));
  Multiplexer #(.enable("false")) multiplexer_12 (.in0(BGTZ), .in1(1'b0), .out(multiplexer_12_out), .sel(rst));
  Multiplexer #(.width(5), .enable("false")) multiplexer_13 (
    .in0(rAaddr), .in1({5{1'b0}}), .out(multiplexer_13_out), .sel(rst));
  Multiplexer #(.width(5), .enable("false")) multiplexer_14 (
    .in0(rBaddr), .in1({5{1'b0}}), .out(multiplexer_14_out), .sel(rst));
  Multiplexer #(.enable("false")) multiplexer_15 (.in0(wEPC), .in1(1'b0), .out(multiplexer_15_out), .sel(rst));
  Multiplexer #(.enable("false")) multiplexer_16 (.in0(wINT), .in1(1'b0), .out(multiplexer_16_out), .sel(rst));
  Multiplexer #(.enable("false")) multiplexer_17 (.in0(ERET), .in1(1'b0), .out(multiplexer_17_out), .sel(rst));
  Register #(.width(32)) register_1 (.D(multiplexer_1_out), .en(not_1_out), .Q(RAout), .clk(clk));  // open: clr
  Register #(.width(32)) register_2 (.D(multiplexer_2_out), .en(not_1_out), .Q(RBout), .clk(clk));  // open: clr
  Register #(.width(32)) register_3 (.D(multiplexer_3_out), .en(not_1_out), .Q(OFFsetout), .clk(clk));  // open: clr
  Register #(.width(32)) register_4 (.D(multiplexer_4_out), .en(not_1_out), .Q(PCout), .clk(clk));  // open: clr
  Register #(.width(4)) register_5 (.D(multiplexer_5_out), .en(not_1_out), .Q(ALUOPout), .clk(clk));  // open: clr
  Register #(.width(1)) register_6 (.D(multiplexer_6_out), .en(not_1_out), .Q(WEout), .clk(clk));  // open: clr
  Register #(.width(1)) register_7 (.D(multiplexer_7_out), .en(not_1_out), .Q(SWout), .clk(clk));  // open: clr
  Register #(.width(1)) register_8 (.D(multiplexer_8_out), .en(not_1_out), .Q(LWout), .clk(clk));  // open: clr
  Register #(.width(26)) register_9 (.D(multiplexer_9_out), .en(not_1_out), .Q(INDEXout), .clk(clk));  // open: clr
  Register #(.width(1)) register_10 (.D(multiplexer_10_out), .en(not_1_out), .Q(JR_2), .clk(clk));  // open: clr
  Register #(.width(1)) register_11 (.D(multiplexer_11_out), .en(not_1_out), .Q(MFLO_2), .clk(clk));  // open: clr
  Register #(.width(1)) register_12 (.D(multiplexer_12_out), .en(not_1_out), .Q(BGTZ_2), .clk(clk));  // open: clr
  Register #(.width(5)) register_13 (.D(multiplexer_13_out), .en(not_1_out), .Q(rAaddr_2), .clk(clk));  // open: clr
  Register #(.width(5)) register_14 (.D(multiplexer_14_out), .en(not_1_out), .Q(rBaddr_2), .clk(clk));  // open: clr
  Register #(.width(1)) register_15 (.D(multiplexer_15_out), .en(not_1_out), .Q(wEPC_2), .clk(clk));  // open: clr
  Register #(.width(1)) register_16 (.D(multiplexer_16_out), .en(not_1_out), .Q(wINT_2), .clk(clk));  // open: clr
  Register #(.width(1)) register_17 (.D(multiplexer_17_out), .en(not_1_out), .Q(ERET_2), .clk(clk));  // open: clr
  Multiplexer #(.width(5), .enable("false")) multiplexer_18 (
    .in0(RDin), .in1({5{1'b0}}), .out(multiplexer_18_out), .sel(rst));
  Multiplexer #(.width(5), .enable("false")) multiplexer_19 (
    .in0(RTin), .in1({5{1'b0}}), .out(multiplexer_19_out), .sel(rst));
  Multiplexer #(.enable("false")) multiplexer_20 (.in0(_16ExtImmin), .in1(1'b0), .out(multiplexer_20_out), .sel(rst));
  Multiplexer #(.enable("false")) multiplexer_21 (.in0(SextImmin), .in1(1'b0), .out(multiplexer_21_out), .sel(rst));
  Multiplexer #(.enable("false")) multiplexer_22 (.in0(JALin), .in1(1'b0), .out(multiplexer_22_out), .sel(rst));
  Multiplexer #(.enable("false")) multiplexer_23 (.in0(_5extImmin), .in1(1'b0), .out(multiplexer_23_out), .sel(rst));
  Multiplexer #(.enable("false")) multiplexer_24 (.in0(SYSin), .in1(1'b0), .out(multiplexer_24_out), .sel(rst));
  Multiplexer #(.enable("false")) multiplexer_25 (.in0(BEQ), .in1(1'b0), .out(multiplexer_25_out), .sel(rst));
  Multiplexer #(.enable("false")) multiplexer_26 (.in0(BNE), .in1(1'b0), .out(multiplexer_26_out), .sel(rst));
  Multiplexer #(.enable("false")) multiplexer_27 (.in0(J), .in1(1'b0), .out(multiplexer_27_out), .sel(rst));
  Multiplexer #(.enable("false")) multiplexer_28 (.in0(MULTU), .in1(1'b0), .out(multiplexer_28_out), .sel(rst));
  Multiplexer #(.enable("false")) multiplexer_29 (.in0(SH), .in1(1'b0), .out(multiplexer_29_out), .sel(rst));
  Multiplexer #(.width(2), .enable("false")) multiplexer_30 (
    .in0(SRC), .in1(2'b00), .out(multiplexer_30_out), .sel(rst));
  Multiplexer #(.enable("false")) multiplexer_31 (.in0(rEPC), .in1(1'b0), .out(multiplexer_31_out), .sel(rst));
  Multiplexer #(.enable("false")) multiplexer_32 (.in0(rINT), .in1(1'b0), .out(multiplexer_32_out), .sel(rst));
  Multiplexer #(.enable("false")) multiplexer_33 (.in0(MFC), .in1(1'b0), .out(multiplexer_33_out), .sel(rst));
  Multiplexer #(.width(5), .enable("false")) multiplexer_34 (
    .in0(RD), .in1({5{1'b0}}), .out(multiplexer_34_out), .sel(rst));
  Register #(.width(5)) register_18 (
    .D(multiplexer_18_out), .en(not_1_out), .Q(register_18_q), .clk(clk));  // open: clr
  Register #(.width(5)) register_19 (
    .D(multiplexer_19_out), .en(not_1_out), .Q(register_19_q), .clk(clk));  // open: clr
  Register #(.width(1)) register_20 (.D(multiplexer_20_out), .en(not_1_out), .Q(_16ExtImmout), .clk(clk));  // open: clr
  Register #(.width(1)) register_21 (.D(multiplexer_21_out), .en(not_1_out), .Q(SextImmout), .clk(clk));  // open: clr
  Register #(.width(1)) register_22 (.D(multiplexer_22_out), .en(not_1_out), .Q(JALout), .clk(clk));  // open: clr
  Register #(.width(1)) register_23 (.D(multiplexer_23_out), .en(not_1_out), .Q(_5extImmout), .clk(clk));  // open: clr
  Register #(.width(1)) register_24 (.D(multiplexer_24_out), .en(not_1_out), .Q(SYSout), .clk(clk));  // open: clr
  Register #(.width(1)) register_25 (.D(multiplexer_25_out), .en(not_1_out), .Q(BEQ_2), .clk(clk));  // open: clr
  Register #(.width(1)) register_26 (.D(multiplexer_26_out), .en(not_1_out), .Q(BNE_2), .clk(clk));  // open: clr
  Register #(.width(1)) register_27 (.D(multiplexer_27_out), .en(not_1_out), .Q(J_2), .clk(clk));  // open: clr
  Register #(.width(1)) register_28 (.D(multiplexer_28_out), .en(not_1_out), .Q(MULTU_2), .clk(clk));  // open: clr
  Register #(.width(1)) register_29 (.D(multiplexer_29_out), .en(not_1_out), .Q(SH_2), .clk(clk));  // open: clr
  Register #(.width(2)) register_30 (.D(multiplexer_30_out), .en(not_1_out), .Q(SRC_2), .clk(clk));  // open: clr
  Register #(.width(1)) register_31 (.D(multiplexer_31_out), .en(not_1_out), .Q(rEPC_2), .clk(clk));  // open: clr
  Register #(.width(1)) register_32 (.D(multiplexer_32_out), .en(not_1_out), .Q(rINT_2), .clk(clk));  // open: clr
  Register #(.width(1)) register_33 (.D(multiplexer_33_out), .en(not_1_out), .Q(MFC_2), .clk(clk));  // open: clr
  Register #(.width(5)) register_34 (.D(multiplexer_34_out), .en(not_1_out), .Q(RD_2), .clk(clk));  // open: clr
  Multiplexer #(.select(2), .width(5), .enable("false")) multiplexer_35 (
    .in0(register_18_q), .in1(register_19_q), .in2({5{1'b1}}), .in3({5{1'b0}}), .out(multiplexer_35_out),
    .sel({JALout, or_1_out[0]}));
  or or_1 (or_1_out[0], _16ExtImmout, SextImmout);
  Multiplexer #(.width(5), .enable("false")) multiplexer_36 (
    .in0(multiplexer_35_out), .in1(5'b10000), .out(DESout), .sel(or_2_out));
  or or_2 (or_2_out, rEPC_2, rINT_2);

  // Other names for the same wires on the sheet: rEPC_t = rEPC_2; rINT_t = rINT_2
endmodule

module EX_MEM (
  input  [31:0] R2in,
  input  [31:0] Rin,
  input  [31:0] RBin,
  input  [31:0] PCin,
  input  [4:0] DESin,
  input  SWin,
  input  ERET,
  input  LWin,
  input  wEPC,
  input  wINT,
  input  JALin,
  input  WEin,
  input  rEPC,
  input  SYSin,
  input  rINT,
  input  MULTU,
  input  MFC,
  input  MFLO,
  input  [4:0] RD,
  input  SH,
  input  [31:0] RA,
  input  clk,
  input  rst,
  input  halt,
  output [31:0] R2out,
  output [31:0] Rout,
  output [31:0] RBout,
  output [31:0] PCout,
  output [4:0] DESout,
  output SWout,
  output ERET_2,
  output LWout,
  output wEPC_2,
  output wINT_2,
  output JALout,
  output WEout,
  output rEPC_2,
  output SYSout,
  output rINT_2,
  output MULTU_2,
  output MFC_2,
  output MFLO_2,
  output [4:0] RD_2,
  output SH_2,
  output [31:0] RA_2
);

  wire multiplexer_6_out, multiplexer_7_out, multiplexer_8_out, multiplexer_9_out, multiplexer_10_out,
       multiplexer_11_out, multiplexer_12_out, multiplexer_13_out, multiplexer_15_out, multiplexer_16_out,
       multiplexer_17_out, multiplexer_18_out, multiplexer_19_out, multiplexer_20_out, not_1_out;
  wire [4:0] multiplexer_5_out, multiplexer_21_out;
  wire [31:0] multiplexer_1_out, multiplexer_2_out, multiplexer_3_out, multiplexer_4_out, multiplexer_14_out;

  not not_1 (not_1_out, halt);
  Multiplexer #(.width(32), .enable("false")) multiplexer_1 (
    .in0(R2in), .in1({32{1'b0}}), .out(multiplexer_1_out), .sel(rst));
  Multiplexer #(.width(32), .enable("false")) multiplexer_2 (
    .in0(Rin), .in1({32{1'b0}}), .out(multiplexer_2_out), .sel(rst));
  Multiplexer #(.width(32), .enable("false")) multiplexer_3 (
    .in0(RBin), .in1({32{1'b0}}), .out(multiplexer_3_out), .sel(rst));
  Multiplexer #(.width(32), .enable("false")) multiplexer_4 (
    .in0(PCin), .in1({32{1'b0}}), .out(multiplexer_4_out), .sel(rst));
  Multiplexer #(.width(5), .enable("false")) multiplexer_5 (
    .in0(DESin), .in1({5{1'b0}}), .out(multiplexer_5_out), .sel(rst));
  Multiplexer #(.enable("false")) multiplexer_6 (.in0(SWin), .in1(1'b0), .out(multiplexer_6_out), .sel(rst));
  Multiplexer #(.enable("false")) multiplexer_7 (.in0(LWin), .in1(1'b0), .out(multiplexer_7_out), .sel(rst));
  Multiplexer #(.enable("false")) multiplexer_8 (.in0(JALin), .in1(1'b0), .out(multiplexer_8_out), .sel(rst));
  Multiplexer #(.enable("false")) multiplexer_9 (.in0(WEin), .in1(1'b0), .out(multiplexer_9_out), .sel(rst));
  Multiplexer #(.enable("false")) multiplexer_10 (.in0(SYSin), .in1(1'b0), .out(multiplexer_10_out), .sel(rst));
  Multiplexer #(.enable("false")) multiplexer_11 (.in0(MULTU), .in1(1'b0), .out(multiplexer_11_out), .sel(rst));
  Multiplexer #(.enable("false")) multiplexer_12 (.in0(MFLO), .in1(1'b0), .out(multiplexer_12_out), .sel(rst));
  Multiplexer #(.enable("false")) multiplexer_13 (.in0(SH), .in1(1'b0), .out(multiplexer_13_out), .sel(rst));
  Multiplexer #(.width(32), .enable("false")) multiplexer_14 (
    .in0(RA), .in1({32{1'b0}}), .out(multiplexer_14_out), .sel(rst));
  Register #(.width(32)) register_1 (.D(multiplexer_1_out), .en(not_1_out), .Q(R2out), .clk(clk));  // open: clr
  Register #(.width(32)) register_2 (.D(multiplexer_2_out), .en(not_1_out), .Q(Rout), .clk(clk));  // open: clr
  Register #(.width(32)) register_3 (.D(multiplexer_3_out), .en(not_1_out), .Q(RBout), .clk(clk));  // open: clr
  Register #(.width(32)) register_4 (.D(multiplexer_4_out), .en(not_1_out), .Q(PCout), .clk(clk));  // open: clr
  Register #(.width(5)) register_5 (.D(multiplexer_5_out), .en(not_1_out), .Q(DESout), .clk(clk));  // open: clr
  Register #(.width(1)) register_6 (.D(multiplexer_6_out), .en(not_1_out), .Q(SWout), .clk(clk));  // open: clr
  Register #(.width(1)) register_7 (.D(multiplexer_7_out), .en(not_1_out), .Q(LWout), .clk(clk));  // open: clr
  Register #(.width(1)) register_8 (.D(multiplexer_8_out), .en(not_1_out), .Q(JALout), .clk(clk));  // open: clr
  Register #(.width(1)) register_9 (.D(multiplexer_9_out), .en(not_1_out), .Q(WEout), .clk(clk));  // open: clr
  Register #(.width(1)) register_10 (.D(multiplexer_10_out), .en(not_1_out), .Q(SYSout), .clk(clk));  // open: clr
  Register #(.width(1)) register_11 (.D(multiplexer_11_out), .en(not_1_out), .Q(MULTU_2), .clk(clk));  // open: clr
  Register #(.width(1)) register_12 (.D(multiplexer_12_out), .en(not_1_out), .Q(MFLO_2), .clk(clk));  // open: clr
  Register #(.width(1)) register_13 (.D(multiplexer_13_out), .en(not_1_out), .Q(SH_2), .clk(clk));  // open: clr
  Register #(.width(32)) register_14 (.D(multiplexer_14_out), .en(not_1_out), .Q(RA_2), .clk(clk));  // open: clr
  Multiplexer #(.enable("false")) multiplexer_15 (.in0(ERET), .in1(1'b0), .out(multiplexer_15_out), .sel(rst));
  Multiplexer #(.enable("false")) multiplexer_16 (.in0(wEPC), .in1(1'b0), .out(multiplexer_16_out), .sel(rst));
  Multiplexer #(.enable("false")) multiplexer_17 (.in0(wINT), .in1(1'b0), .out(multiplexer_17_out), .sel(rst));
  Multiplexer #(.enable("false")) multiplexer_18 (.in0(rEPC), .in1(1'b0), .out(multiplexer_18_out), .sel(rst));
  Multiplexer #(.enable("false")) multiplexer_19 (.in0(rINT), .in1(1'b0), .out(multiplexer_19_out), .sel(rst));
  Multiplexer #(.enable("false")) multiplexer_20 (.in0(MFC), .in1(1'b0), .out(multiplexer_20_out), .sel(rst));
  Multiplexer #(.width(5), .enable("false")) multiplexer_21 (
    .in0(RD), .in1({5{1'b0}}), .out(multiplexer_21_out), .sel(rst));
  Register #(.width(1)) register_15 (.D(multiplexer_15_out), .en(not_1_out), .Q(ERET_2), .clk(clk));  // open: clr
  Register #(.width(1)) register_16 (.D(multiplexer_16_out), .en(not_1_out), .Q(wEPC_2), .clk(clk));  // open: clr
  Register #(.width(1)) register_17 (.D(multiplexer_17_out), .en(not_1_out), .Q(wINT_2), .clk(clk));  // open: clr
  Register #(.width(1)) register_18 (.D(multiplexer_18_out), .en(not_1_out), .Q(rEPC_2), .clk(clk));  // open: clr
  Register #(.width(1)) register_19 (.D(multiplexer_19_out), .en(not_1_out), .Q(rINT_2), .clk(clk));  // open: clr
  Register #(.width(1)) register_20 (.D(multiplexer_20_out), .en(not_1_out), .Q(MFC_2), .clk(clk));  // open: clr
  Register #(.width(5)) register_21 (.D(multiplexer_21_out), .en(not_1_out), .Q(RD_2), .clk(clk));  // open: clr
endmodule

module MEM_WB (
  input  [31:0] INT32,
  input  [31:0] EPC,
  input  [31:0] R2in,
  input  [31:0] Rin,
  input  [31:0] DATAin,
  input  [31:0] PCin,
  input  [4:0] DESin,
  input  LWin,
  input  ERET,
  input  JALin,
  input  wEPC,
  input  wINT,
  input  WEin,
  input  rEPC,
  input  SYSin,
  input  MULTU,
  input  rINT,
  input  MFC,
  input  MFLO,
  input  [4:0] RD,
  input  [31:0] RA,
  input  clk,
  input  rst,
  input  halt,
  output [31:0] PC,
  output [31:0] R2out,
  output [31:0] Rout,
  output [31:0] Wout,
  output [4:0] rWin,
  output ERET_2,
  output wEPC_2,
  output wINT_2,
  output WEout,
  output rEPC_2,
  output SYSout,
  output MULTU_2,
  output rINT_2,
  output MFC_2,
  output MFLO_2,
  output [4:0] RD_2,
  output [31:0] RA_2
);

  wire multiplexer_9_out, multiplexer_10_out, multiplexer_11_out, multiplexer_12_out, multiplexer_13_out,
       multiplexer_14_out, multiplexer_18_out, multiplexer_19_out, multiplexer_20_out, multiplexer_21_out,
       multiplexer_22_out, multiplexer_23_out, not_1_out;
  wire [1:0] register_9_q;
  wire [4:0] multiplexer_8_out, multiplexer_24_out;
  wire [31:0] adder_1_out, EPC_t, INT32_t, multiplexer_1_out, multiplexer_2_out, multiplexer_3_out,
       multiplexer_4_out, multiplexer_5_out, multiplexer_6_out, multiplexer_7_out, multiplexer_15_out,
       multiplexer_16_out, register_6_q, register_7_q;

  not not_1 (not_1_out, halt);
  Adder #(.width(32)) adder_1 (.a(PCin), .b(32'h4), .out(adder_1_out));  // open: cin, cout
  Register #(.width(32)) register_1 (.D(multiplexer_1_out), .Q(INT32_t), .clk(clk));  // open: en, clr
  Multiplexer #(.width(32), .enable("false")) multiplexer_1 (
    .in0(INT32), .in1({32{1'b0}}), .out(multiplexer_1_out), .sel(rst));
  Multiplexer #(.width(32), .enable("false")) multiplexer_2 (
    .in0(EPC), .in1({32{1'b0}}), .out(multiplexer_2_out), .sel(rst));
  Register #(.width(32)) register_2 (.D(multiplexer_2_out), .Q(EPC_t), .clk(clk));  // open: en, clr
  Multiplexer #(.width(32), .enable("false")) multiplexer_3 (
    .in0(PCin), .in1({32{1'b0}}), .out(multiplexer_3_out), .sel(rst));
  Register #(.width(32)) register_3 (.D(multiplexer_3_out), .en(not_1_out), .Q(PC), .clk(clk));  // open: clr
  Register #(.width(32)) register_4 (.D(multiplexer_4_out), .en(not_1_out), .Q(R2out), .clk(clk));  // open: clr
  Multiplexer #(.width(32), .enable("false")) multiplexer_4 (
    .in0(R2in), .in1({32{1'b0}}), .out(multiplexer_4_out), .sel(rst));
  Register #(.width(32)) register_5 (.D(multiplexer_5_out), .en(not_1_out), .Q(Rout), .clk(clk));  // open: clr
  Multiplexer #(.width(32), .enable("false")) multiplexer_5 (
    .in0(Rin), .in1({32{1'b0}}), .out(multiplexer_5_out), .sel(rst));
  Multiplexer #(.width(32), .enable("false")) multiplexer_6 (
    .in0(DATAin), .in1({32{1'b0}}), .out(multiplexer_6_out), .sel(rst));
  Register #(.width(32)) register_6 (.D(multiplexer_6_out), .en(not_1_out), .Q(register_6_q), .clk(clk));  // open: clr
  Multiplexer #(.width(32), .enable("false")) multiplexer_7 (
    .in0(adder_1_out), .in1({32{1'b0}}), .out(multiplexer_7_out), .sel(rst));
  Register #(.width(32)) register_7 (.D(multiplexer_7_out), .en(not_1_out), .Q(register_7_q), .clk(clk));  // open: clr
  Register #(.width(5)) register_8 (.D(multiplexer_8_out), .en(not_1_out), .Q(rWin), .clk(clk));  // open: clr
  Multiplexer #(.width(5), .enable("false")) multiplexer_8 (
    .in0(DESin), .in1({5{1'b0}}), .out(multiplexer_8_out), .sel(rst));
  Multiplexer #(.enable("false")) multiplexer_9 (.in0(LWin), .in1(1'b0), .out(multiplexer_9_out), .sel(rst));
  Register #(.width(1)) register_9 (
    .D(multiplexer_9_out), .en(not_1_out), .Q(register_9_q[0]), .clk(clk));  // open: clr
  Multiplexer #(.enable("false")) multiplexer_10 (.in0(JALin), .in1(1'b0), .out(multiplexer_10_out), .sel(rst));
  Register #(.width(1)) register_10 (
    .D(multiplexer_10_out), .en(not_1_out), .Q(register_9_q[1]), .clk(clk));  // open: clr
  Multiplexer #(.enable("false")) multiplexer_11 (.in0(WEin), .in1(1'b0), .out(multiplexer_11_out), .sel(rst));
  Register #(.width(1)) register_11 (.D(multiplexer_11_out), .en(not_1_out), .Q(WEout), .clk(clk));  // open: clr
  Register #(.width(1)) register_12 (.D(multiplexer_12_out), .en(not_1_out), .Q(SYSout), .clk(clk));  // open: clr
  Multiplexer #(.enable("false")) multiplexer_12 (.in0(SYSin), .in1(1'b0), .out(multiplexer_12_out), .sel(rst));
  Multiplexer #(.enable("false")) multiplexer_13 (.in0(MULTU), .in1(1'b0), .out(multiplexer_13_out), .sel(rst));
  Register #(.width(1)) register_13 (.D(multiplexer_13_out), .en(not_1_out), .Q(MULTU_2), .clk(clk));  // open: clr
  Register #(.width(1)) register_14 (.D(multiplexer_14_out), .en(not_1_out), .Q(MFLO_2), .clk(clk));  // open: clr
  Multiplexer #(.enable("false")) multiplexer_14 (.in0(MFLO), .in1(1'b0), .out(multiplexer_14_out), .sel(rst));
  Multiplexer #(.width(32), .enable("false")) multiplexer_15 (
    .in0(RA), .in1({32{1'b0}}), .out(multiplexer_15_out), .sel(rst));
  Register #(.width(32)) register_15 (.D(multiplexer_15_out), .en(not_1_out), .Q(RA_2), .clk(clk));  // open: clr
  Multiplexer #(.select(2), .width(32), .disabled(0), .enable("false")) multiplexer_16 (
    .in0(Rout), .in1(register_6_q), .in2(register_7_q), .in3({32{1'b0}}), .out(multiplexer_16_out),
    .sel(register_9_q));
  Multiplexer #(.select(2), .width(32), .disabled(0), .enable("false")) multiplexer_17 (
    .in0(multiplexer_16_out), .in1(EPC_t), .in2(INT32_t), .out(Wout), .sel({rINT_2, rEPC_2}));  // open: in3
  Multiplexer #(.enable("false")) multiplexer_18 (.in0(ERET), .in1(1'b0), .out(multiplexer_18_out), .sel(rst));
  Multiplexer #(.enable("false")) multiplexer_19 (.in0(wEPC), .in1(1'b0), .out(multiplexer_19_out), .sel(rst));
  Multiplexer #(.enable("false")) multiplexer_20 (.in0(wINT), .in1(1'b0), .out(multiplexer_20_out), .sel(rst));
  Multiplexer #(.enable("false")) multiplexer_21 (.in0(rEPC), .in1(1'b0), .out(multiplexer_21_out), .sel(rst));
  Multiplexer #(.enable("false")) multiplexer_22 (.in0(rINT), .in1(1'b0), .out(multiplexer_22_out), .sel(rst));
  Multiplexer #(.enable("false")) multiplexer_23 (.in0(MFC), .in1(1'b0), .out(multiplexer_23_out), .sel(rst));
  Multiplexer #(.width(5), .enable("false")) multiplexer_24 (
    .in0(RD), .in1({5{1'b0}}), .out(multiplexer_24_out), .sel(rst));
  Register #(.width(1)) register_16 (.D(multiplexer_18_out), .en(not_1_out), .Q(ERET_2), .clk(clk));  // open: clr
  Register #(.width(1)) register_17 (.D(multiplexer_19_out), .en(not_1_out), .Q(wEPC_2), .clk(clk));  // open: clr
  Register #(.width(1)) register_18 (.D(multiplexer_20_out), .en(not_1_out), .Q(wINT_2), .clk(clk));  // open: clr
  Register #(.width(1)) register_19 (.D(multiplexer_21_out), .en(not_1_out), .Q(rEPC_2), .clk(clk));  // open: clr
  Register #(.width(1)) register_20 (.D(multiplexer_22_out), .en(not_1_out), .Q(rINT_2), .clk(clk));  // open: clr
  Register #(.width(1)) register_21 (.D(multiplexer_23_out), .en(not_1_out), .Q(MFC_2), .clk(clk));  // open: clr
  Register #(.width(5)) register_22 (.D(multiplexer_24_out), .en(not_1_out), .Q(RD_2), .clk(clk));  // open: clr

  // Other names for the same wires on the sheet: rEPC_t = rEPC_2; rINT_t = rINT_2; PC_t[31:0] = PCin
endmodule

module Handler (
  input  [4:0] DES1,
  input  [4:0] rA,
  input  WE1,
  input  [4:0] rB,
  input  [1:0] SRC,
  input  wEPC,
  input  wINT,
  input  LW,
  output Result
);

  wire and_1_out, and_2_out, and_3_out, and_4_out, and_5_out, comparator_1_eq, comparator_2_eq,
       comparator_3_eq, comparator_4_eq, not_1_out, not_2_out, result_t;
  wire [4:0] Dnum1, Snum1, Snum2;

  Comparator #(.width(5)) comparator_1 (.a(Dnum1), .b(Snum1), .eq(comparator_1_eq));  // open: gt, lt
  Comparator #(.width(5)) comparator_2 (.a(Snum1), .b({5{1'b0}}), .eq(comparator_2_eq));  // open: gt, lt
  not not_1 (not_1_out, comparator_2_eq);
  Comparator #(.width(5)) comparator_3 (.a(Dnum1), .b(Snum2), .eq(comparator_3_eq));  // open: gt, lt
  not not_2 (not_2_out, comparator_4_eq);
  Comparator #(.width(5)) comparator_4 (.a(Snum2), .b({5{1'b0}}), .eq(comparator_4_eq));  // open: gt, lt
  Multiplexer #(.width(5), .enable("false")) multiplexer_1 (.in0({5{1'b0}}), .in1(DES1), .out(Dnum1), .sel(WE1));
  and and_1 (and_1_out, comparator_1_eq, not_1_out);
  and and_2 (and_2_out, comparator_3_eq, not_2_out);
  or or_1 (result_t, and_1_out, and_2_out);
  Multiplexer #(.width(5), .enable("false")) multiplexer_2 (.in0({5{1'b0}}), .in1(rA), .out(Snum1), .sel(SRC[1]));
  Multiplexer #(.width(5), .enable("false")) multiplexer_3 (.in0({5{1'b0}}), .in1(rB), .out(Snum2), .sel(SRC[0]));
  and and_3 (and_3_out, wEPC, LW);
  and and_4 (and_4_out, result_t, LW);
  and and_5 (and_5_out, LW, wINT);
  or or_2 (Result, and_3_out, and_4_out, and_5_out);

  // Notes on the sheet:
  //   结果为0，不插气泡
endmodule

module Branch (
  input  [31:0] PC,
  input  [31:0] OFFSET,
  input  [25:0] ins_index,
  input  [31:0] RA,
  input  JAL,
  input  JR,
  input  J,
  input  [31:0] RB,
  input  BGTZ,
  input  BNE,
  input  BEQ,
  input  clk,
  output [31:0] NextPC,
  output [15:0] un,
  output choice,
  output [15:0] success
);

  wire and_1_out, and_2_out, and_3_out, comparator_1_eq, comparator_1_gt, not_1_out, or_4_out;
  wire [1:0] or_1_out;
  wire [31:0] adder_1_out, adder_2_out, multiplexer_1_out, multiplexer_2_out;

  Multiplexer #(.width(32), .enable("false")) multiplexer_1 (
    .in0(RB), .in1({32{1'b0}}), .out(multiplexer_1_out), .sel(BGTZ));
  Comparator #(.width(32)) comparator_1 (
    .a(RA), .b(multiplexer_1_out), .gt(comparator_1_gt), .eq(comparator_1_eq));  // open: lt
  and and_1 (and_1_out, BGTZ, comparator_1_gt);
  not not_1 (not_1_out, comparator_1_eq);
  Adder #(.width(32)) adder_1 (.a(PC), .b(32'h4), .out(adder_1_out));  // open: cin, cout
  Multiplexer #(.width(32), .enable("false")) multiplexer_2 (
    .in0({PC[31:28], ins_index, 2'b00}), .in1(RA), .out(multiplexer_2_out), .sel(JR));
  and and_2 (and_2_out, not_1_out, BNE);
  and and_3 (and_3_out, comparator_1_eq, BEQ);
  Adder #(.width(32)) adder_2 (.a(adder_1_out), .b({OFFSET[29:0], 2'b00}), .out(adder_2_out));  // open: cin, cout
  or or_1 (or_1_out[0], and_1_out, and_2_out, and_3_out);
  or or_2 (or_1_out[1], JR, J, JAL);
  Multiplexer #(.select(2), .width(32), .enable("false")) multiplexer_3 (
    .in0(adder_1_out), .in1(adder_2_out), .in2(multiplexer_2_out), .in3({32{1'b0}}), .out(NextPC),
    .sel(or_1_out));
  // Probe on NextPC
  or or_3 (choice, JAL, J, JR, or_1_out[0]);
  or or_4 (or_4_out, JAL, J, JR);
  Counter #(.width(16), .max('hffff)) counter_1 (.count(or_4_out), .Q(un), .clk(clk));  // open: load, D, carry, clr
  Counter #(.width(16), .max('hffff)) counter_2 (
    .count(or_1_out[0]), .Q(success), .clk(clk));  // open: load, D, carry, clr
endmodule

// Stcs
module Statistics (
  input  stall,
  input  [31:0] RAsys,
  input  syscall,
  input  clk,
  input  [31:0] RB,
  input  disp,
  input  Go,
  input  [31:0] RA,
  output pause,
  output [15:0] \总周期数 ,
  output halt,
  output [15:0] \插入气泡数 ,
  output [31:0] SyscallOut
);

  wire and_1_out, and_2_out, and_4_out, comparator_1_eq, comparator_2_eq, comparator_3_eq, comparator_4_eq,
       d_ff_1_qn, not_1_out, not_2_out, not_3_out, not_4_out, not_5_out, or_1_out, or_2_out, or_3_out;
  wire [15:0] adder_1_out, bit_extender_1_out;

  assign bit_extender_1_out = {{15{1'b0}}, stall};  // Bit_Extender bit_extender_1
  or or_1 (or_1_out, pause, halt);
  and and_1 (and_1_out, disp, not_2_out);
  or or_2 (or_2_out, pause, halt);
  not not_1 (not_1_out, or_2_out);
  D_Flip_Flop d_ff_1 (.clk(clk), .D(or_1_out), .Qn(d_ff_1_qn));  // open: Q, preset, en, reset
  Register #(.width(32)) a0 (.D(RB), .en(and_1_out), .Q(SyscallOut), .clk(clk));  // open: clr
  not not_2 (not_2_out, and_2_out);
  Adder #(.width(16)) adder_1 (.a(bit_extender_1_out), .b(\插入气泡数 ), .out(adder_1_out));  // open: cin, cout
  Register #(.width(16)) register_1 (.D(adder_1_out), .en(not_1_out), .Q(\插入气泡数 ), .clk(clk));  // open: clr
  Counter #(.width(16), .max('hffff)) counter_1 (
    .count(d_ff_1_qn), .Q(\总周期数 ), .clk(clk));  // open: load, D, carry, clr
  Comparator #(.width(32)) comparator_1 (.a(32'h22), .b(RA), .eq(comparator_1_eq));  // open: gt, lt
  not not_3 (not_3_out, comparator_1_eq);
  and and_2 (and_2_out, not_3_out, disp);
  Comparator #(.width(32)) comparator_2 (.a(32'h32), .b(RAsys), .eq(comparator_2_eq));  // open: gt, lt
  Comparator #(.width(32)) comparator_3 (.a(32'h22), .b(RAsys), .eq(comparator_3_eq));  // open: gt, lt
  Comparator #(.width(32)) comparator_4 (.a(32'h32), .b(RAsys), .eq(comparator_4_eq));  // open: gt, lt
  or or_3 (or_3_out, comparator_2_eq, comparator_3_eq);
  not not_4 (not_4_out, or_3_out);
  and and_3 (halt, not_4_out, syscall);
  not not_5 (not_5_out, Go);
  and and_4 (and_4_out, comparator_4_eq, syscall);
  and and_5 (pause, not_5_out, and_4_out);
endmodule

module Redirection (
  input  [31:0] RA,
  input  [31:0] wMEM,
  input  [31:0] RB,
  input  [31:0] wWB,
  input  _5ext,
  input  [31:0] Offset,
  input  ext,
  input  [31:0] WB_R,
  input  [3:0] ALUop,
  input  mflo,
  input  wEPC,
  input  wINT,
  input  [4:0] rA_2,
  input  [4:0] DES1,
  input  WE1,
  input  [4:0] rB_2,
  input  [4:0] DES2,
  input  WE2,
  input  [1:0] SRC,
  output [31:0] Result1,
  output [31:0] RAout,
  output [31:0] Result2,
  output [31:0] RBout
);

  wire or_1_out;
  wire [2:0] comparator_1_eq, comparator_4_eq, comparator_7_eq, comparator_10_eq;
  wire [4:0] Dnum1, Dnum2, multiplexer_10_out, multiplexer_13_out, Snum1, Snum2;
  wire [31:0] multiplexer_1_out, multiplexer_4_out, multiplexer_6_out, multiplexer_11_out,
       multiplexer_12_out, multiplexer_14_out, multiplexer_15_out, multiplexer_16_out, multiplexer_17_out;

  Comparator #(.width(5)) comparator_1 (.a(Snum1), .b(Dnum2), .eq(comparator_1_eq[0]));  // open: gt, lt
  Comparator #(.width(5)) comparator_2 (.a(Snum1), .b(Dnum1), .eq(comparator_1_eq[1]));  // open: gt, lt
  Comparator #(.width(5)) comparator_3 (.a(Snum1), .b({5{1'b0}}), .eq(comparator_1_eq[2]));  // open: gt, lt
  Multiplexer #(.width(32), .enable("false")) multiplexer_1 (
    .in0(wMEM), .in1(WB_R), .out(multiplexer_1_out), .sel(mflo));
  Multiplexer #(.width(5), .enable("false")) multiplexer_2 (.in0({5{1'b0}}), .in1(rA_2), .out(Snum1), .sel(SRC[1]));
  Multiplexer #(.width(5), .enable("false")) multiplexer_3 (.in0({5{1'b0}}), .in1(rB_2), .out(Snum2), .sel(SRC[0]));
  Multiplexer #(.select(3), .width(32), .enable("false")) multiplexer_4 (
    .in0(RA), .in1(wWB), .in2(multiplexer_1_out), .in3(multiplexer_1_out), .in4(RA), .in5(RA), .in6(RA),
    .in7(RA), .out(multiplexer_4_out), .sel(comparator_1_eq));
  Multiplexer #(.width(32), .enable("false")) multiplexer_5 (
    .in0(multiplexer_4_out), .in1(wWB), .out(RAout), .sel(or_1_out));
  or or_1 (or_1_out, wEPC, wINT);
  Comparator #(.width(5)) comparator_4 (.a(Snum2), .b(Dnum2), .eq(comparator_4_eq[0]));  // open: gt, lt
  Comparator #(.width(5)) comparator_5 (.a(Snum2), .b(Dnum1), .eq(comparator_4_eq[1]));  // open: gt, lt
  Comparator #(.width(5)) comparator_6 (.a(Snum2), .b({5{1'b0}}), .eq(comparator_4_eq[2]));  // open: gt, lt
  Multiplexer #(.width(32), .enable("false")) multiplexer_6 (
    .in0(wMEM), .in1(WB_R), .out(multiplexer_6_out), .sel(mflo));
  Multiplexer #(.width(5), .enable("false")) multiplexer_7 (.in0({5{1'b0}}), .in1(DES1), .out(Dnum1), .sel(WE1));
  Multiplexer #(.width(5), .enable("false")) multiplexer_8 (.in0({5{1'b0}}), .in1(DES2), .out(Dnum2), .sel(WE2));
  Multiplexer #(.select(3), .width(32), .enable("false")) multiplexer_9 (
    .in0(RB), .in1(wWB), .in2(multiplexer_6_out), .in3(multiplexer_6_out), .in4(RB), .in5(RB), .in6(RB),
    .in7(RB), .out(RBout), .sel(comparator_4_eq));
  Multiplexer #(.width(5), .enable("false")) multiplexer_10 (
    .in0(Snum1), .in1(Snum2), .out(multiplexer_10_out), .sel(_5ext));
  Multiplexer #(.width(32), .enable("false")) multiplexer_11 (
    .in0(RA), .in1(RB), .out(multiplexer_11_out), .sel(_5ext));
  Multiplexer #(.width(32), .enable("false")) multiplexer_12 (
    .in0(wMEM), .in1(WB_R), .out(multiplexer_12_out), .sel(mflo));
  Multiplexer #(.width(5), .enable("false")) multiplexer_13 (
    .in0(Snum2), .in1({5{1'b0}}), .out(multiplexer_13_out), .sel(ext));
  Multiplexer #(.width(32), .enable("false")) multiplexer_14 (
    .in0(RB), .in1(Offset), .out(multiplexer_14_out), .sel(ext));
  Multiplexer #(.width(32), .enable("false")) multiplexer_15 (
    .in0(wMEM), .in1(WB_R), .out(multiplexer_15_out), .sel(mflo));
  Comparator #(.width(5)) comparator_7 (.a(Dnum2), .b(multiplexer_10_out), .eq(comparator_7_eq[0]));  // open: gt, lt
  Comparator #(.width(5)) comparator_8 (.a(Dnum1), .b(multiplexer_10_out), .eq(comparator_7_eq[1]));  // open: gt, lt
  Comparator #(.width(5)) comparator_9 (
    .a(multiplexer_10_out), .b({5{1'b0}}), .eq(comparator_7_eq[2]));  // open: gt, lt
  Multiplexer #(.select(3), .width(32), .enable("false")) multiplexer_16 (
    .in0(multiplexer_11_out), .in1(wWB), .in2(multiplexer_12_out), .in3(multiplexer_12_out),
    .in4(multiplexer_11_out), .in5(multiplexer_11_out), .in6(multiplexer_11_out), .in7(multiplexer_11_out),
    .out(multiplexer_16_out), .sel(comparator_7_eq));
  Comparator #(.width(5)) comparator_10 (.a(Dnum2), .b(multiplexer_13_out), .eq(comparator_10_eq[0]));  // open: gt, lt
  Comparator #(.width(5)) comparator_11 (.a(Dnum1), .b(multiplexer_13_out), .eq(comparator_10_eq[1]));  // open: gt, lt
  Comparator #(.width(5)) comparator_12 (
    .a(multiplexer_13_out), .b({5{1'b0}}), .eq(comparator_10_eq[2]));  // open: gt, lt
  Multiplexer #(.select(3), .width(32), .enable("false")) multiplexer_17 (
    .in0(multiplexer_14_out), .in1(wWB), .in2(multiplexer_15_out), .in3(multiplexer_15_out),
    .in4(multiplexer_14_out), .in5(multiplexer_14_out), .in6(multiplexer_14_out), .in7(multiplexer_14_out),
    .out(multiplexer_17_out), .sel(comparator_10_eq));
  // ALU alu_1: pin names not known; wires that end beside it: multiplexer_16_out, multiplexer_17_out, ALUop, Result1, Result2
endmodule
